// Logisim project MadDrFrankComputerDemo500.circ as structural Verilog: 45 circuits, main circuit main
module main (
);

  wire and_1_out, and_2_out, and_3_out, and_4_out, clock_1_out, clock_2_out, clock_3_out, clock_4_out,
       clock_5_out, clock_6_out, clock_7_out, comparator_1_eq, comparator_1_gt, comparator_1_lt, not_1_out,
       not_2_out, or_1_out, or_2_out, or_3_out, or_4_out, or_5_out, plex_1_out_2, plex_1_out_3, plex_1_out_4,
       plex_1_out_5, plex_1_out_6, plex_1_out_7, plex_1_out_8, plex_1_out_9;
  wire [15:0] adder_1_out, controlled_buffer_1_out, controlled_buffer_3_out, counter_1_q, ram_1_dout,
       random_1_out, register_1_q, register_2_q, rom_1_data, rom_2_data, rom_3_data, rom_4_data, rom_5_data;

  ROM #(.addrWidth(16), .dataWidth(16)) rom_1 (.addr(counter_1_q), .data(rom_1_data));
  Counter #(.max('hffff), .width(16)) counter_1 (
    .load(or_1_out), .clk(clock_1_out), .D(rom_1_data), .Q(counter_1_q));  // open: clr, up, count, carry
  Clock clock_1 (.out(clock_1_out));
  or or_1 (or_1_out, and_1_out, and_4_out, plex_1_out_3);
  ROM #(.addrWidth(16), .dataWidth(16)) rom_2 (.addr(counter_1_q), .data(rom_2_data));
  ROM #(.addrWidth(16), .dataWidth(16)) rom_3 (.addr(counter_1_q), .data(rom_3_data));
  and and_1 (and_1_out, and_2_out, and_3_out);
  ROM #(.addrWidth(16), .dataWidth(16)) rom_4 (.addr(counter_1_q), .data(rom_4_data));
  Clock clock_2 (.out(clock_2_out));
  Clock clock_3 (.out(clock_3_out));
  PLEX plex_1 (
    .in_1(rom_2_data), .out_2(plex_1_out_2), .out_3(plex_1_out_3), .out_4(plex_1_out_4),
    .out_5(plex_1_out_5), .out_6(plex_1_out_6), .out_7(plex_1_out_7), .out_8(plex_1_out_8),
    .out_9(plex_1_out_9));  // open: out_10
  Register #(.width(16)) register_1 (
    .D(rom_3_data), .en(plex_1_out_4), .clk(clock_2_out), .Q(register_1_q));  // open: clr
  Register #(.width(16)) register_2 (
    .D(rom_4_data), .en(plex_1_out_4), .clk(clock_3_out), .Q(register_2_q));  // open: clr
  and and_2 (and_2_out, comparator_1_eq, plex_1_out_8);
  and and_3 (and_3_out, comparator_1_lt, plex_1_out_6);
  and and_4 (and_4_out, comparator_1_gt, plex_1_out_7);
  or or_2 (or_2_out, plex_1_out_6, plex_1_out_7, plex_1_out_8, plex_1_out_9);
  or or_3 (or_3_out, plex_1_out_2, plex_1_out_3, plex_1_out_4, plex_1_out_6, plex_1_out_7, plex_1_out_8, plex_1_out_5);
  Random #(.width(16)) random_1 (.clr(clock_4_out), .next(clock_5_out), .clk(clock_6_out), .out(random_1_out));
  Clock clock_4 (.out(clock_4_out));
  Clock clock_5 (.out(clock_5_out));
  Clock clock_6 (.out(clock_6_out));
  not not_1 (not_1_out, or_3_out);
  assign controlled_buffer_1_out = not_1_out ? random_1_out : 16'bz;  // Controlled_Buffer controlled_buffer_1
  or or_4 (or_4_out, plex_1_out_3, plex_1_out_2, plex_1_out_4);
  assign controlled_buffer_1_out = or_3_out ? adder_1_out : 16'bz;  // Controlled_Buffer controlled_buffer_2
  or or_5 (or_5_out, or_4_out, or_2_out);
  ROM #(.addrWidth(16), .dataWidth(16)) rom_5 (.addr(counter_1_q), .data(rom_5_data));
  assign controlled_buffer_3_out = or_5_out ? controlled_buffer_1_out : 16'bz;  // Controlled_Buffer controlled_buffer_3
  not not_2 (not_2_out, or_5_out);
  assign controlled_buffer_3_out = not_2_out ? {16{1'b0}} : 16'bz;  // Controlled_Buffer controlled_buffer_4
  RAM #(.addrWidth(16), .dataWidth(16)) ram_1 (
    .addr(register_2_q), .we(1'b1), .oe(1'b1), .clk(clock_7_out), .din(controlled_buffer_3_out),
    .dout(ram_1_dout));
  Clock clock_7 (.out(clock_7_out));
  Adder #(.width(16)) adder_1 (.a(register_1_q), .b(ram_1_dout), .out(adder_1_out));  // open: cin, cout
  Comparator #(.width(16)) comparator_1 (
    .a(rom_5_data), .b(adder_1_out), .gt(comparator_1_gt), .eq(comparator_1_eq), .lt(comparator_1_lt));
  LED led_1 (.in(comparator_1_gt));
  LED led_2 (.in(comparator_1_lt));
  LED led_3 (.in(comparator_1_eq));

  // Notes on the sheet:
  //   contents of rom_2 (hex, n*v repeats v):
  //   4*2 3 0 7 7 1
  //   contents of rom_3 (hex, n*v repeats v):
  //   1 1 1 0 0 0 1
  //   contents of rom_4 (hex, n*v repeats v):
  //   8*1
  //   contents of rom_5 (hex, n*v repeats v):
  //   8*1
endmodule

module PLEX (
  input  [15:0] in_1,
  output out_2,
  output out_3,
  output out_4,
  output out_5,
  output out_6,
  output out_7,
  output out_8,
  output out_9,
  output out_10
);

  Comparator #(.width(16)) comparator_1 (.a(in_1), .b({16{1'b0}}), .eq(out_2));  // open: gt, lt
  Comparator #(.width(16)) comparator_2 (.a(in_1), .b(16'h1), .eq(out_3));  // open: gt, lt
  Comparator #(.width(16)) comparator_3 (.a(in_1), .b(16'h2), .eq(out_4));  // open: gt, lt
  Comparator #(.width(16)) comparator_4 (.a(in_1), .b(16'h3), .eq(out_5));  // open: gt, lt
  Comparator #(.width(16)) comparator_5 (.a(in_1), .b(16'h4), .eq(out_6));  // open: gt, lt
  Comparator #(.width(16)) comparator_6 (.a(in_1), .b(16'h5), .eq(out_7));  // open: gt, lt
  Comparator #(.width(16)) comparator_7 (.a(in_1), .b(16'h6), .eq(out_8));  // open: gt, lt
  Comparator #(.width(16)) comparator_8 (.a(in_1), .b(16'h7), .eq(out_9));  // open: gt, lt
  Comparator #(.width(16)) comparator_9 (.a(in_1), .b(16'h8), .eq(out_10));  // open: gt, lt
endmodule

module ALIMENTATOR (
  input  [15:0] in_1,
  input  in_2,
  output [15:0] out_3
);

  wire clock_1_out;
  wire [15:0] register_1_q, register_2_q;

  Clock clock_1 (.out(clock_1_out));
  Register #(.width(16)) register_1 (.D(in_1), .en(clock_1_out), .clk(clock_1_out), .Q(register_1_q));  // open: clr
  Register #(.width(16)) register_2 (.D(out_3), .en(clock_1_out), .clk(clock_1_out), .Q(register_2_q), .clr(in_2));
  Adder #(.width(16)) adder_1 (.a(register_1_q), .b(register_2_q), .out(out_3));  // open: cin, cout
endmodule

module PC1 (
  input  in_1,
  output [15:0] out_2
);

  wire clock_1_out, comparator_1_eq;
  wire [15:0] counter_1_q, register_1_q, register_2_q, rom_1_data, rom_2_data;

  Clock clock_1 (.out(clock_1_out));
  Counter #(.max('hffff), .width(16)) counter_1 (
    .load(comparator_1_eq), .clk(clock_1_out), .D(rom_1_data), .Q(counter_1_q));  // open: clr, up, count, carry
  ROM #(.addrWidth(16), .dataWidth(16)) rom_1 (.addr(counter_1_q), .data(rom_1_data));
  Register #(.width(16)) register_1 (
    .D(rom_1_data), .en(clock_1_out), .clk(clock_1_out), .Q(register_1_q));  // open: clr
  Register #(.width(16)) register_2 (.D(out_2), .en(clock_1_out), .clk(clock_1_out), .Q(register_2_q), .clr(in_1));
  ROM #(.addrWidth(16), .dataWidth(16)) rom_2 (.addr(counter_1_q), .data(rom_2_data));
  Adder #(.width(16)) adder_1 (.a(register_1_q), .b(register_2_q), .out(out_2));  // open: cin, cout
  Comparator #(.width(16)) comparator_1 (.a(16'h1), .b(rom_2_data), .eq(comparator_1_eq));  // open: gt, lt

  // Notes on the sheet:
  //   contents of rom_1 (hex, n*v repeats v):
  //   1 3 1
  //   contents of rom_2 (hex, n*v repeats v):
  //   0 0 0 1
endmodule

module PC2 (
);

  wire clock_1_out, comparator_1_eq, comparator_2_eq;
  wire [15:0] adder_1_out, counter_1_q, register_1_q, register_2_q, rom_1_data, rom_2_data;

  Counter #(.max('hffff), .width(16)) counter_1 (
    .load(comparator_1_eq), .clk(clock_1_out), .D(rom_1_data), .Q(counter_1_q));  // open: clr, up, count, carry
  Clock clock_1 (.out(clock_1_out));
  ROM #(.addrWidth(16), .dataWidth(16)) rom_1 (.addr(counter_1_q), .data(rom_1_data));
  Register #(.width(16)) register_1 (
    .D(rom_1_data), .en(clock_1_out), .clk(clock_1_out), .Q(register_1_q));  // open: clr
  Register #(.width(16)) register_2 (
    .D(adder_1_out), .en(clock_1_out), .clk(clock_1_out), .Q(register_2_q), .clr(comparator_2_eq));
  ROM #(.addrWidth(16), .dataWidth(16)) rom_2 (.addr(counter_1_q), .data(rom_2_data));
  Adder #(.width(16)) adder_1 (.a(register_1_q), .b(register_2_q), .out(adder_1_out));  // open: cin, cout
  Comparator #(.width(16)) comparator_1 (.a(16'h1), .b(rom_2_data), .eq(comparator_1_eq));  // open: gt, lt
  Comparator #(.width(16)) comparator_2 (.a(16'h2), .b(rom_2_data), .eq(comparator_2_eq));  // open: gt, lt

  // Notes on the sheet:
  //   contents of rom_1 (hex, n*v repeats v):
  //   5*1
  //   contents of rom_2 (hex, n*v repeats v):
  //   5*0 2 1
endmodule

module PC3 (
);

  wire clock_1_out, comparator_1_eq, comparator_2_eq;
  wire [15:0] adder_1_out, counter_1_q, register_1_q, register_2_q, rom_1_data, rom_2_data;

  Clock clock_1 (.out(clock_1_out));
  Counter #(.max('hffff), .width(16)) counter_1 (
    .load(comparator_1_eq), .clk(clock_1_out), .D(rom_1_data), .Q(counter_1_q));  // open: clr, up, count, carry
  ROM #(.addrWidth(16), .dataWidth(16)) rom_1 (.addr(counter_1_q), .data(rom_1_data));
  Register #(.width(16)) register_1 (
    .D(rom_1_data), .en(clock_1_out), .clk(clock_1_out), .Q(register_1_q));  // open: clr
  Register #(.width(16)) register_2 (
    .D(adder_1_out), .en(clock_1_out), .clk(clock_1_out), .Q(register_2_q), .clr(comparator_2_eq));
  ROM #(.addrWidth(16), .dataWidth(16)) rom_2 (.addr(counter_1_q), .data(rom_2_data));
  Adder #(.width(16)) adder_1 (.a(register_1_q), .b(register_2_q), .out(adder_1_out));  // open: cin, cout
  Comparator #(.width(16)) comparator_1 (.a(16'h1), .b(rom_2_data), .eq(comparator_1_eq));  // open: gt, lt
  Comparator #(.width(16)) comparator_2 (.a(16'h2), .b(rom_2_data), .eq(comparator_2_eq));  // open: gt, lt

  // Notes on the sheet:
  //   contents of rom_1 (hex, n*v repeats v):
  //   5*1
  //   contents of rom_2 (hex, n*v repeats v):
  //   5*0 2 1
endmodule

module PC4 (
);

  wire clock_1_out, plex_1_out_3, plex_1_out_4;
  wire [15:0] adder_1_out, counter_1_q, register_1_q, register_2_q, rom_1_data, rom_2_data;

  Clock clock_1 (.out(clock_1_out));
  Counter #(.max('hffff), .width(16)) counter_1 (
    .load(plex_1_out_3), .clk(clock_1_out), .D(rom_1_data), .Q(counter_1_q));  // open: clr, up, count, carry
  ROM #(.addrWidth(16), .dataWidth(16)) rom_1 (.addr(counter_1_q), .data(rom_1_data));
  Register #(.width(16)) register_1 (
    .D(rom_1_data), .en(clock_1_out), .clk(clock_1_out), .Q(register_1_q));  // open: clr
  Register #(.width(16)) register_2 (
    .D(adder_1_out), .en(clock_1_out), .clk(clock_1_out), .Q(register_2_q), .clr(plex_1_out_4));
  ROM #(.addrWidth(16), .dataWidth(16)) rom_2 (.addr(counter_1_q), .data(rom_2_data));
  Adder #(.width(16)) adder_1 (.a(register_1_q), .b(register_2_q), .out(adder_1_out));  // open: cin, cout
  PLEX plex_1 (
    .in_1(rom_2_data), .out_3(plex_1_out_3), .out_4(plex_1_out_4));  // open: out_2, out_5, out_6, out_7, out_8, out_9, out_10

  // Notes on the sheet:
  //   contents of rom_1 (hex, n*v repeats v):
  //   5*1
  //   contents of rom_2 (hex, n*v repeats v):
  //   5*0 2 1
endmodule

module PC5 (
);

  wire clock_1_out, plex_1_out_3, plex_1_out_4;
  wire [15:0] adder_1_out, counter_1_q, register_1_q, register_2_q, rom_1_data, rom_2_data;

  Clock clock_1 (.out(clock_1_out));
  Counter #(.max('hffff), .width(16)) counter_1 (
    .load(plex_1_out_3), .clk(clock_1_out), .D(rom_1_data), .Q(counter_1_q));  // open: clr, up, count, carry
  ROM #(.addrWidth(16), .dataWidth(16)) rom_1 (.addr(counter_1_q), .data(rom_1_data));
  Register #(.width(16)) register_1 (
    .D(rom_1_data), .en(clock_1_out), .clk(clock_1_out), .Q(register_1_q));  // open: clr
  Register #(.width(16)) register_2 (
    .D(adder_1_out), .en(clock_1_out), .clk(clock_1_out), .Q(register_2_q), .clr(plex_1_out_4));
  ROM #(.addrWidth(16), .dataWidth(16)) rom_2 (.addr(counter_1_q), .data(rom_2_data));
  Adder #(.width(16)) adder_1 (.a(register_1_q), .b(register_2_q), .out(adder_1_out));  // open: cin, cout
  PLEX plex_1 (
    .in_1(rom_2_data), .out_3(plex_1_out_3), .out_4(plex_1_out_4));  // open: out_2, out_5, out_6, out_7, out_8, out_9, out_10

  // Notes on the sheet:
  //   contents of rom_1 (hex, n*v repeats v):
  //   5*1
  //   contents of rom_2 (hex, n*v repeats v):
  //   5*0 2 1
endmodule

module PC8 (
);

  wire clock_1_out, plex_1_out_3, plex_1_out_4, plex_1_out_5;
  wire [15:0] adder_1_out, counter_1_q, register_1_q, register_2_q, rom_1_data, rom_2_data;

  Clock clock_1 (.out(clock_1_out));
  Counter #(.max('hffff), .width(16)) counter_1 (
    .load(plex_1_out_3), .clk(clock_1_out), .D(rom_1_data), .Q(counter_1_q));  // open: clr, up, count, carry
  ROM #(.addrWidth(16), .dataWidth(16)) rom_1 (.addr(counter_1_q), .data(rom_1_data));
  Register #(.width(16)) register_1 (
    .D(rom_1_data), .en(plex_1_out_5), .clk(clock_1_out), .Q(register_1_q));  // open: clr
  Register #(.width(16)) register_2 (
    .D(adder_1_out), .en(plex_1_out_5), .clk(clock_1_out), .Q(register_2_q), .clr(plex_1_out_4));
  ROM #(.addrWidth(16), .dataWidth(16)) rom_2 (.addr(counter_1_q), .data(rom_2_data));
  Adder #(.width(16)) adder_1 (.a(register_1_q), .b(register_2_q), .out(adder_1_out));  // open: cin, cout
  PLEX plex_1 (
    .in_1(rom_2_data), .out_3(plex_1_out_3), .out_4(plex_1_out_4), .out_5(plex_1_out_5));  // open: out_2, out_6, out_7, out_8, out_9, out_10

  // Notes on the sheet:
  //   contents of rom_1 (hex, n*v repeats v):
  //   5*1
  //   contents of rom_2 (hex, n*v repeats v):
  //   5*3 2 1
endmodule

module PC10 (
);

  wire clock_1_out, plex_1_out_3, plex_1_out_4, plex_1_out_5;
  wire [15:0] adder_1_out, counter_1_q, register_1_q, register_2_q, rom_1_data, rom_2_data;

  Counter #(.max('hffff), .width(16)) counter_1 (
    .load(plex_1_out_3), .clk(clock_1_out), .D(rom_1_data), .Q(counter_1_q));  // open: clr, up, count, carry
  Clock clock_1 (.out(clock_1_out));
  ROM #(.addrWidth(16), .dataWidth(16)) rom_1 (.addr(counter_1_q), .data(rom_1_data));
  Register #(.width(16)) register_1 (
    .D(rom_1_data), .en(plex_1_out_5), .clk(clock_1_out), .Q(register_1_q));  // open: clr
  Register #(.width(16)) register_2 (
    .D(adder_1_out), .en(plex_1_out_5), .clk(clock_1_out), .Q(register_2_q), .clr(plex_1_out_4));
  ROM #(.addrWidth(16), .dataWidth(16)) rom_2 (.addr(counter_1_q), .data(rom_2_data));
  Adder #(.width(16)) adder_1 (.a(register_1_q), .b(register_2_q), .out(adder_1_out));  // open: cin, cout
  PLEX plex_1 (
    .in_1(rom_2_data), .out_3(plex_1_out_3), .out_4(plex_1_out_4), .out_5(plex_1_out_5));  // open: out_2, out_6, out_7, out_8, out_9, out_10

  // Notes on the sheet:
  //   contents of rom_1 (hex, n*v repeats v):
  //   5*1
  //   contents of rom_2 (hex, n*v repeats v):
  //   5*3 2 1
endmodule

module PC15 (
);

  wire clock_1_out, plex_1_out_3, plex_1_out_4, plex_1_out_5;
  wire [15:0] adder_1_out, counter_1_q, register_1_q, register_2_q, rom_1_data, rom_2_data;

  Counter #(.max('hffff), .width(16)) counter_1 (
    .load(plex_1_out_3), .clk(clock_1_out), .D(rom_1_data), .Q(counter_1_q));  // open: clr, up, count, carry
  Clock clock_1 (.out(clock_1_out));
  ROM #(.addrWidth(16), .dataWidth(16)) rom_1 (.addr(counter_1_q), .data(rom_1_data));
  Register #(.width(16)) register_1 (
    .D(rom_1_data), .en(plex_1_out_5), .clk(clock_1_out), .Q(register_1_q));  // open: clr
  Register #(.width(16)) register_2 (
    .D(adder_1_out), .en(plex_1_out_5), .clk(clock_1_out), .Q(register_2_q));  // open: clr
  ROM #(.addrWidth(16), .dataWidth(16)) rom_2 (.addr(counter_1_q), .data(rom_2_data));
  Adder #(.width(16)) adder_1 (.a(register_1_q), .b(register_2_q), .out(adder_1_out));  // open: cin, cout
  PLEX plex_1 (
    .in_1(rom_2_data), .out_3(plex_1_out_3), .out_4(plex_1_out_4), .out_5(plex_1_out_5));  // open: out_2, out_6, out_7, out_8, out_9, out_10

  // Notes on the sheet:
  //   contents of rom_1 (hex, n*v repeats v):
  //   5*1
  //   contents of rom_2 (hex, n*v repeats v):
  //   5*3 2 1
endmodule

module PC20 (
);

  wire clock_1_out, plex_1_out_3, plex_1_out_4, plex_1_out_5;
  wire [15:0] adder_1_out, counter_1_q, register_1_q, register_2_q, rom_1_data, rom_2_data;

  Clock clock_1 (.out(clock_1_out));
  Counter #(.max('hffff), .width(16)) counter_1 (
    .load(plex_1_out_3), .clk(clock_1_out), .D(rom_1_data), .Q(counter_1_q));  // open: clr, up, count, carry
  ROM #(.addrWidth(16), .dataWidth(16)) rom_1 (.addr(counter_1_q), .data(rom_1_data));
  Register #(.width(16)) register_1 (
    .D(rom_1_data), .en(plex_1_out_5), .clk(clock_1_out), .Q(register_1_q));  // open: clr
  Register #(.width(16)) register_2 (
    .D(adder_1_out), .en(plex_1_out_5), .clk(clock_1_out), .Q(register_2_q), .clr(plex_1_out_4));
  ROM #(.addrWidth(16), .dataWidth(16)) rom_2 (.addr(counter_1_q), .data(rom_2_data));
  Adder #(.width(16)) adder_1 (.a(register_1_q), .b(register_2_q), .out(adder_1_out));  // open: cin, cout
  PLEX plex_1 (
    .in_1(rom_2_data), .out_3(plex_1_out_3), .out_4(plex_1_out_4), .out_5(plex_1_out_5));  // open: out_2, out_6, out_7, out_8, out_9, out_10

  // Notes on the sheet:
  //   contents of rom_1 (hex, n*v repeats v):
  //   5*1
  //   contents of rom_2 (hex, n*v repeats v):
  //   5*3 2 1
endmodule

module ALIMENTATOR2 (
);

  wire clock_1_out, clock_2_out, clock_3_out, clock_4_out, plex_1_out_3, plex_1_out_4;
  wire [15:0] adder_1_out, counter_1_q, ram_1_dout, register_1_q, register_2_q, rom_1_data, rom_2_data,
       rom_3_data, rom_4_data;

  ROM #(.addrWidth(16), .dataWidth(16)) rom_1 (.addr(counter_1_q), .data(rom_1_data));
  Counter #(.max('hffff), .width(16)) counter_1 (
    .load(plex_1_out_3), .clk(clock_1_out), .D(rom_1_data), .Q(counter_1_q));  // open: clr, up, count, carry
  Clock clock_1 (.out(clock_1_out));
  ROM #(.addrWidth(16), .dataWidth(16)) rom_2 (.addr(counter_1_q), .data(rom_2_data));
  ROM #(.addrWidth(16), .dataWidth(16)) rom_3 (.addr(counter_1_q), .data(rom_3_data));
  ROM #(.addrWidth(16), .dataWidth(16)) rom_4 (.addr(counter_1_q), .data(rom_4_data));
  PLEX plex_1 (
    .in_1(rom_2_data), .out_3(plex_1_out_3), .out_4(plex_1_out_4));  // open: out_2, out_5, out_6, out_7, out_8, out_9, out_10
  Register #(.width(16)) register_1 (
    .D(rom_3_data), .en(plex_1_out_4), .clk(clock_2_out), .Q(register_1_q));  // open: clr
  Clock clock_2 (.out(clock_2_out));
  Register #(.width(16)) register_2 (
    .D(rom_4_data), .en(plex_1_out_4), .clk(clock_3_out), .Q(register_2_q));  // open: clr
  Clock clock_3 (.out(clock_3_out));
  Clock clock_4 (.out(clock_4_out));
  RAM #(.addrWidth(16), .dataWidth(16)) ram_1 (
    .addr(register_2_q), .we(1'b1), .oe(1'b1), .clk(clock_4_out), .din(adder_1_out), .dout(ram_1_dout));
  Adder #(.width(16)) adder_1 (.a(register_1_q), .b(ram_1_dout), .out(adder_1_out));  // open: cin, cout

  // Notes on the sheet:
  //   contents of rom_2 (hex, n*v repeats v):
  //   4*2 4*0 1
  //   contents of rom_3 (hex, n*v repeats v):
  //   1 1 1
endmodule

module PC25 (
);

  wire clock_1_out, clock_2_out, clock_3_out, clock_4_out, plex_1_out_3, plex_1_out_4;
  wire [15:0] adder_1_out, counter_1_q, ram_1_dout, register_1_q, register_2_q, rom_1_data, rom_2_data,
       rom_3_data, rom_4_data;

  ROM #(.addrWidth(16), .dataWidth(16)) rom_1 (.addr(counter_1_q), .data(rom_1_data));
  Counter #(.max('hffff), .width(16)) counter_1 (
    .load(plex_1_out_3), .clk(clock_1_out), .D(rom_1_data), .Q(counter_1_q));  // open: clr, up, count, carry
  Clock clock_1 (.out(clock_1_out));
  ROM #(.addrWidth(16), .dataWidth(16)) rom_2 (.addr(counter_1_q), .data(rom_2_data));
  ROM #(.addrWidth(16), .dataWidth(16)) rom_3 (.addr(counter_1_q), .data(rom_3_data));
  ROM #(.addrWidth(16), .dataWidth(16)) rom_4 (.addr(counter_1_q), .data(rom_4_data));
  Clock clock_2 (.out(clock_2_out));
  Clock clock_3 (.out(clock_3_out));
  PLEX plex_1 (
    .in_1(rom_2_data), .out_3(plex_1_out_3), .out_4(plex_1_out_4));  // open: out_2, out_5, out_6, out_7, out_8, out_9, out_10
  Register #(.width(16)) register_1 (
    .D(rom_3_data), .en(plex_1_out_4), .clk(clock_2_out), .Q(register_1_q));  // open: clr
  Register #(.width(16)) register_2 (
    .D(rom_4_data), .en(plex_1_out_4), .clk(clock_3_out), .Q(register_2_q));  // open: clr
  Clock clock_4 (.out(clock_4_out));
  RAM #(.addrWidth(16), .dataWidth(16)) ram_1 (
    .addr(register_2_q), .we(1'b1), .oe(1'b1), .clk(clock_4_out), .din(adder_1_out), .dout(ram_1_dout));
  Adder #(.width(16)) adder_1 (.a(register_1_q), .b(ram_1_dout), .out(adder_1_out));  // open: cin, cout

  // Notes on the sheet:
  //   contents of rom_2 (hex, n*v repeats v):
  //   4*2 4*0 1
  //   contents of rom_3 (hex, n*v repeats v):
  //   1 1 1
endmodule

module PC30 (
);

  wire clock_1_out, clock_2_out, clock_3_out, clock_4_out, plex_1_out_3, plex_1_out_4;
  wire [15:0] adder_1_out, counter_1_q, ram_1_dout, register_1_q, register_2_q, rom_1_data, rom_2_data,
       rom_3_data, rom_4_data;

  Clock clock_1 (.out(clock_1_out));
  ROM #(.addrWidth(16), .dataWidth(16)) rom_1 (.addr(counter_1_q), .data(rom_1_data));
  Counter #(.max('hffff), .width(16)) counter_1 (
    .load(plex_1_out_3), .clk(clock_1_out), .D(rom_1_data), .Q(counter_1_q));  // open: clr, up, count, carry
  ROM #(.addrWidth(16), .dataWidth(16)) rom_2 (.addr(counter_1_q), .data(rom_2_data));
  ROM #(.addrWidth(16), .dataWidth(16)) rom_3 (.addr(counter_1_q), .data(rom_3_data));
  ROM #(.addrWidth(16), .dataWidth(16)) rom_4 (.addr(counter_1_q), .data(rom_4_data));
  Register #(.width(16)) register_1 (
    .D(rom_2_data), .en(plex_1_out_4), .clk(clock_2_out), .Q(register_1_q));  // open: clr
  Clock clock_2 (.out(clock_2_out));
  Register #(.width(16)) register_2 (
    .D(rom_4_data), .en(plex_1_out_4), .clk(clock_3_out), .Q(register_2_q));  // open: clr
  Clock clock_3 (.out(clock_3_out));
  PLEX plex_1 (
    .in_1(rom_3_data), .out_3(plex_1_out_3), .out_4(plex_1_out_4));  // open: out_2, out_5, out_6, out_7, out_8, out_9, out_10
  Clock clock_4 (.out(clock_4_out));
  RAM #(.addrWidth(16), .dataWidth(16)) ram_1 (
    .addr(register_2_q), .we(1'b1), .oe(1'b1), .clk(clock_4_out), .din(adder_1_out), .dout(ram_1_dout));
  Adder #(.width(16)) adder_1 (.a(register_1_q), .b(ram_1_dout), .out(adder_1_out));  // open: cin, cout

  // Notes on the sheet:
  //   contents of rom_2 (hex, n*v repeats v):
  //   1 1 1
  //   contents of rom_3 (hex, n*v repeats v):
  //   4*2 4*0 1
  //   contents of rom_4 (hex, n*v repeats v):
  //   8*1
endmodule

module PC35 (
);

  wire clock_1_out, clock_2_out, clock_3_out, clock_4_out, or_1_out, plex_1_out_2, plex_1_out_3, plex_1_out_4;
  wire [15:0] adder_1_out, controlled_buffer_1_out, counter_1_q, ram_1_dout, register_1_q, register_2_q,
       rom_1_data, rom_2_data, rom_3_data, rom_4_data;

  ROM #(.addrWidth(16), .dataWidth(16)) rom_1 (.addr(counter_1_q), .data(rom_1_data));
  Counter #(.max('hffff), .width(16)) counter_1 (
    .load(plex_1_out_3), .clk(clock_1_out), .D(rom_1_data), .Q(counter_1_q));  // open: clr, up, count, carry
  Clock clock_1 (.out(clock_1_out));
  ROM #(.addrWidth(16), .dataWidth(16)) rom_2 (.addr(counter_1_q), .data(rom_2_data));
  ROM #(.addrWidth(16), .dataWidth(16)) rom_3 (.addr(counter_1_q), .data(rom_3_data));
  ROM #(.addrWidth(16), .dataWidth(16)) rom_4 (.addr(counter_1_q), .data(rom_4_data));
  Clock clock_2 (.out(clock_2_out));
  Clock clock_3 (.out(clock_3_out));
  PLEX plex_1 (
    .in_1(rom_2_data), .out_2(plex_1_out_2), .out_3(plex_1_out_3), .out_4(plex_1_out_4));  // open: out_5, out_6, out_7, out_8, out_9, out_10
  Register #(.width(16)) register_1 (
    .D(rom_3_data), .en(plex_1_out_4), .clk(clock_2_out), .Q(register_1_q));  // open: clr
  Register #(.width(16)) register_2 (
    .D(rom_4_data), .en(plex_1_out_4), .clk(clock_3_out), .Q(register_2_q));  // open: clr
  or or_1 (or_1_out, plex_1_out_3, plex_1_out_2, plex_1_out_4);
  assign controlled_buffer_1_out = or_1_out ? adder_1_out : 16'bz;  // Controlled_Buffer controlled_buffer_1
  RAM #(.addrWidth(16), .dataWidth(16)) ram_1 (
    .addr(register_2_q), .we(1'b1), .oe(1'b1), .clk(clock_4_out), .din(controlled_buffer_1_out),
    .dout(ram_1_dout));
  Clock clock_4 (.out(clock_4_out));
  Adder #(.width(16)) adder_1 (.a(register_1_q), .b(ram_1_dout), .out(adder_1_out));  // open: cin, cout

  // Notes on the sheet:
  //   contents of rom_2 (hex, n*v repeats v):
  //   4*2 4*0 1
  //   contents of rom_3 (hex, n*v repeats v):
  //   1 1 1
  //   contents of rom_4 (hex, n*v repeats v):
  //   8*1
endmodule

module PC40 (
);

  wire clock_1_out, clock_2_out, clock_3_out, clock_4_out, or_1_out, plex_1_out_2, plex_1_out_3, plex_1_out_4;
  wire [15:0] adder_1_out, controlled_buffer_1_out, counter_1_q, ram_1_dout, register_1_q, register_2_q,
       rom_1_data, rom_2_data, rom_3_data, rom_4_data;

  ROM #(.addrWidth(16), .dataWidth(16)) rom_1 (.addr(counter_1_q), .data(rom_1_data));
  Clock clock_1 (.out(clock_1_out));
  Counter #(.max('hffff), .width(16)) counter_1 (
    .load(plex_1_out_3), .clk(clock_1_out), .D(rom_1_data), .Q(counter_1_q));  // open: clr, up, count, carry
  ROM #(.addrWidth(16), .dataWidth(16)) rom_2 (.addr(counter_1_q), .data(rom_2_data));
  ROM #(.addrWidth(16), .dataWidth(16)) rom_3 (.addr(counter_1_q), .data(rom_3_data));
  ROM #(.addrWidth(16), .dataWidth(16)) rom_4 (.addr(counter_1_q), .data(rom_4_data));
  PLEX plex_1 (
    .in_1(rom_2_data), .out_2(plex_1_out_2), .out_3(plex_1_out_3), .out_4(plex_1_out_4));  // open: out_5, out_6, out_7, out_8, out_9, out_10
  Register #(.width(16)) register_1 (
    .D(rom_3_data), .en(plex_1_out_4), .clk(clock_2_out), .Q(register_1_q));  // open: clr
  Clock clock_2 (.out(clock_2_out));
  Register #(.width(16)) register_2 (
    .D(rom_4_data), .en(plex_1_out_4), .clk(clock_3_out), .Q(register_2_q));  // open: clr
  Clock clock_3 (.out(clock_3_out));
  or or_1 (or_1_out, plex_1_out_3, plex_1_out_2, plex_1_out_4);
  assign controlled_buffer_1_out = or_1_out ? adder_1_out : 16'bz;  // Controlled_Buffer controlled_buffer_1
  Clock clock_4 (.out(clock_4_out));
  RAM #(.addrWidth(16), .dataWidth(16)) ram_1 (
    .addr(register_2_q), .we(1'b1), .oe(1'b1), .clk(clock_4_out), .din(controlled_buffer_1_out),
    .dout(ram_1_dout));
  Adder #(.width(16)) adder_1 (.a(register_1_q), .b(ram_1_dout), .out(adder_1_out));  // open: cin, cout

  // Notes on the sheet:
  //   contents of rom_2 (hex, n*v repeats v):
  //   4*2 4*0 1
  //   contents of rom_3 (hex, n*v repeats v):
  //   1 1 1
  //   contents of rom_4 (hex, n*v repeats v):
  //   8*1
endmodule

module PC45 (
);

  wire clock_1_out, clock_2_out, clock_3_out, clock_4_out, or_1_out, plex_1_out_2, plex_1_out_3, plex_1_out_4;
  wire [15:0] adder_1_out, controlled_buffer_1_out, counter_1_q, ram_1_dout, register_1_q, register_2_q,
       rom_1_data, rom_2_data, rom_3_data, rom_4_data;

  ROM #(.addrWidth(16), .dataWidth(16)) rom_1 (.addr(counter_1_q), .data(rom_1_data));
  Counter #(.max('hffff), .width(16)) counter_1 (
    .load(plex_1_out_3), .clk(clock_1_out), .D(rom_1_data), .Q(counter_1_q));  // open: clr, up, count, carry
  Clock clock_1 (.out(clock_1_out));
  ROM #(.addrWidth(16), .dataWidth(16)) rom_2 (.addr(counter_1_q), .data(rom_2_data));
  ROM #(.addrWidth(16), .dataWidth(16)) rom_3 (.addr(counter_1_q), .data(rom_3_data));
  ROM #(.addrWidth(16), .dataWidth(16)) rom_4 (.addr(counter_1_q), .data(rom_4_data));
  Clock clock_2 (.out(clock_2_out));
  Clock clock_3 (.out(clock_3_out));
  PLEX plex_1 (
    .in_1(rom_2_data), .out_2(plex_1_out_2), .out_3(plex_1_out_3), .out_4(plex_1_out_4));  // open: out_5, out_6, out_7, out_8, out_9, out_10
  Register #(.width(16)) register_1 (
    .D(rom_3_data), .en(plex_1_out_4), .clk(clock_2_out), .Q(register_1_q));  // open: clr
  Register #(.width(16)) register_2 (
    .D(rom_4_data), .en(plex_1_out_4), .clk(clock_3_out), .Q(register_2_q));  // open: clr
  assign controlled_buffer_1_out = or_1_out ? adder_1_out : 16'bz;  // Controlled_Buffer controlled_buffer_1
  or or_1 (or_1_out, plex_1_out_3, plex_1_out_2, plex_1_out_4);
  RAM #(.addrWidth(16), .dataWidth(16)) ram_1 (
    .addr(register_2_q), .we(1'b1), .oe(1'b1), .clk(clock_4_out), .din(controlled_buffer_1_out),
    .dout(ram_1_dout));
  Clock clock_4 (.out(clock_4_out));
  Adder #(.width(16)) adder_1 (.a(register_1_q), .b(ram_1_dout), .out(adder_1_out));  // open: cin, cout

  // Notes on the sheet:
  //   contents of rom_2 (hex, n*v repeats v):
  //   4*2 4*0 1
  //   contents of rom_3 (hex, n*v repeats v):
  //   1 1 1
  //   contents of rom_4 (hex, n*v repeats v):
  //   8*1
endmodule

module PC50 (
);

  wire clock_1_out, clock_2_out, clock_3_out, clock_4_out, not_1_out, or_1_out, plex_1_out_2, plex_1_out_3,
       plex_1_out_4;
  wire [15:0] adder_1_out, controlled_buffer_1_out, counter_1_q, ram_1_dout, register_1_q, register_2_q,
       rom_1_data, rom_2_data, rom_3_data, rom_4_data;

  ROM #(.addrWidth(16), .dataWidth(16)) rom_1 (.addr(counter_1_q), .data(rom_1_data));
  Counter #(.max('hffff), .width(16)) counter_1 (
    .load(plex_1_out_3), .clk(clock_1_out), .D(rom_1_data), .Q(counter_1_q));  // open: clr, up, count, carry
  Clock clock_1 (.out(clock_1_out));
  ROM #(.addrWidth(16), .dataWidth(16)) rom_2 (.addr(counter_1_q), .data(rom_2_data));
  ROM #(.addrWidth(16), .dataWidth(16)) rom_3 (.addr(counter_1_q), .data(rom_3_data));
  ROM #(.addrWidth(16), .dataWidth(16)) rom_4 (.addr(counter_1_q), .data(rom_4_data));
  PLEX plex_1 (
    .in_1(rom_2_data), .out_2(plex_1_out_2), .out_3(plex_1_out_3), .out_4(plex_1_out_4));  // open: out_5, out_6, out_7, out_8, out_9, out_10
  Register #(.width(16)) register_1 (
    .D(rom_3_data), .en(plex_1_out_4), .clk(clock_2_out), .Q(register_1_q));  // open: clr
  Clock clock_2 (.out(clock_2_out));
  Register #(.width(16)) register_2 (
    .D(rom_4_data), .en(plex_1_out_4), .clk(clock_3_out), .Q(register_2_q));  // open: clr
  Clock clock_3 (.out(clock_3_out));
  or or_1 (or_1_out, plex_1_out_3, plex_1_out_2, plex_1_out_4);
  assign controlled_buffer_1_out = or_1_out ? adder_1_out : 16'bz;  // Controlled_Buffer controlled_buffer_1
  not not_1 (not_1_out, or_1_out);
  assign controlled_buffer_1_out = not_1_out ? {16{1'b0}} : 16'bz;  // Controlled_Buffer controlled_buffer_2
  RAM #(.addrWidth(16), .dataWidth(16)) ram_1 (
    .addr(register_2_q), .we(1'b1), .oe(1'b1), .clk(clock_4_out), .din(controlled_buffer_1_out),
    .dout(ram_1_dout));
  Clock clock_4 (.out(clock_4_out));
  Adder #(.width(16)) adder_1 (.a(register_1_q), .b(ram_1_dout), .out(adder_1_out));  // open: cin, cout

  // Notes on the sheet:
  //   contents of rom_2 (hex, n*v repeats v):
  //   4*2 3 0 0 0 1
  //   contents of rom_3 (hex, n*v repeats v):
  //   1 1 1
  //   contents of rom_4 (hex, n*v repeats v):
  //   8*1
endmodule

module PC80 (
);

  wire clock_1_out, clock_2_out, clock_3_out, clock_4_out, not_1_out, or_1_out, plex_1_out_2, plex_1_out_3,
       plex_1_out_4;
  wire [15:0] adder_1_out, controlled_buffer_1_out, counter_1_q, ram_1_dout, register_1_q, register_2_q,
       rom_1_data, rom_2_data, rom_3_data, rom_4_data;

  ROM #(.addrWidth(16), .dataWidth(16)) rom_1 (.addr(counter_1_q), .data(rom_1_data));
  Counter #(.max('hffff), .width(16)) counter_1 (
    .load(plex_1_out_3), .clk(clock_1_out), .D(rom_1_data), .Q(counter_1_q));  // open: clr, up, count, carry
  Clock clock_1 (.out(clock_1_out));
  ROM #(.addrWidth(16), .dataWidth(16)) rom_2 (.addr(counter_1_q), .data(rom_2_data));
  ROM #(.addrWidth(16), .dataWidth(16)) rom_3 (.addr(counter_1_q), .data(rom_3_data));
  ROM #(.addrWidth(16), .dataWidth(16)) rom_4 (.addr(counter_1_q), .data(rom_4_data));
  Clock clock_2 (.out(clock_2_out));
  Clock clock_3 (.out(clock_3_out));
  PLEX plex_1 (
    .in_1(rom_2_data), .out_2(plex_1_out_2), .out_3(plex_1_out_3), .out_4(plex_1_out_4));  // open: out_5, out_6, out_7, out_8, out_9, out_10
  Register #(.width(16)) register_1 (
    .D(rom_3_data), .en(plex_1_out_4), .clk(clock_2_out), .Q(register_1_q));  // open: clr
  Register #(.width(16)) register_2 (
    .D(rom_4_data), .en(plex_1_out_4), .clk(clock_3_out), .Q(register_2_q));  // open: clr
  assign controlled_buffer_1_out = or_1_out ? adder_1_out : 16'bz;  // Controlled_Buffer controlled_buffer_1
  or or_1 (or_1_out, plex_1_out_3, plex_1_out_2, plex_1_out_4);
  not not_1 (not_1_out, or_1_out);
  Clock clock_4 (.out(clock_4_out));
  assign controlled_buffer_1_out = not_1_out ? {16{1'b0}} : 16'bz;  // Controlled_Buffer controlled_buffer_2
  RAM #(.addrWidth(16), .dataWidth(16)) ram_1 (
    .addr(register_2_q), .we(1'b1), .oe(1'b1), .clk(clock_4_out), .din(controlled_buffer_1_out),
    .dout(ram_1_dout));
  Adder #(.width(16)) adder_1 (.a(register_1_q), .b(ram_1_dout), .out(adder_1_out));  // open: cin, cout

  // Notes on the sheet:
  //   contents of rom_2 (hex, n*v repeats v):
  //   4*2 3 0 0 0 1
  //   contents of rom_3 (hex, n*v repeats v):
  //   1 1 1
  //   contents of rom_4 (hex, n*v repeats v):
  //   8*1
endmodule

module PC100 (
);

  wire clock_1_out, clock_2_out, clock_3_out, clock_4_out, not_1_out, or_1_out, plex_1_out_2, plex_1_out_3,
       plex_1_out_4;
  wire [15:0] adder_1_out, controlled_buffer_1_out, counter_1_q, ram_1_dout, register_1_q, register_2_q,
       rom_1_data, rom_2_data, rom_3_data, rom_4_data;

  Clock clock_1 (.out(clock_1_out));
  ROM #(.addrWidth(16), .dataWidth(16)) rom_1 (.addr(counter_1_q), .data(rom_1_data));
  Counter #(.max('hffff), .width(16)) counter_1 (
    .load(plex_1_out_3), .clk(clock_1_out), .D(rom_1_data), .Q(counter_1_q));  // open: clr, up, count, carry
  ROM #(.addrWidth(16), .dataWidth(16)) rom_2 (.addr(counter_1_q), .data(rom_2_data));
  ROM #(.addrWidth(16), .dataWidth(16)) rom_3 (.addr(counter_1_q), .data(rom_3_data));
  ROM #(.addrWidth(16), .dataWidth(16)) rom_4 (.addr(counter_1_q), .data(rom_4_data));
  Register #(.width(16)) register_1 (
    .D(rom_2_data), .en(plex_1_out_4), .clk(clock_2_out), .Q(register_1_q));  // open: clr
  Clock clock_2 (.out(clock_2_out));
  Register #(.width(16)) register_2 (
    .D(rom_4_data), .en(plex_1_out_4), .clk(clock_3_out), .Q(register_2_q));  // open: clr
  Clock clock_3 (.out(clock_3_out));
  PLEX plex_1 (
    .in_1(rom_3_data), .out_2(plex_1_out_2), .out_3(plex_1_out_3), .out_4(plex_1_out_4));  // open: out_5, out_6, out_7, out_8, out_9, out_10
  assign controlled_buffer_1_out = or_1_out ? adder_1_out : 16'bz;  // Controlled_Buffer controlled_buffer_1
  or or_1 (or_1_out, plex_1_out_3, plex_1_out_2, plex_1_out_4);
  assign controlled_buffer_1_out = not_1_out ? {16{1'b0}} : 16'bz;  // Controlled_Buffer controlled_buffer_2
  not not_1 (not_1_out, or_1_out);
  Clock clock_4 (.out(clock_4_out));
  RAM #(.addrWidth(16), .dataWidth(16)) ram_1 (
    .addr(register_2_q), .we(1'b1), .oe(1'b1), .clk(clock_4_out), .din(controlled_buffer_1_out),
    .dout(ram_1_dout));
  Adder #(.width(16)) adder_1 (.a(register_1_q), .b(ram_1_dout), .out(adder_1_out));  // open: cin, cout

  // Notes on the sheet:
  //   contents of rom_2 (hex, n*v repeats v):
  //   1 1 1
  //   contents of rom_3 (hex, n*v repeats v):
  //   4*2 3 0 0 0 1
  //   contents of rom_4 (hex, n*v repeats v):
  //   8*1
endmodule

module PC105 (
);

  wire clock_1_out, clock_2_out, clock_3_out, clock_4_out, not_1_out, or_1_out, plex_1_out_2, plex_1_out_3,
       plex_1_out_4;
  wire [15:0] adder_1_out, controlled_buffer_1_out, counter_1_q, ram_1_dout, register_1_q, register_2_q,
       rom_1_data, rom_2_data, rom_3_data, rom_4_data;

  ROM #(.addrWidth(16), .dataWidth(16)) rom_1 (.addr(counter_1_q), .data(rom_1_data));
  Counter #(.max('hffff), .width(16)) counter_1 (
    .load(plex_1_out_3), .clk(clock_1_out), .D(rom_1_data), .Q(counter_1_q));  // open: clr, up, count, carry
  Clock clock_1 (.out(clock_1_out));
  ROM #(.addrWidth(16), .dataWidth(16)) rom_2 (.addr(counter_1_q), .data(rom_2_data));
  ROM #(.addrWidth(16), .dataWidth(16)) rom_3 (.addr(counter_1_q), .data(rom_3_data));
  ROM #(.addrWidth(16), .dataWidth(16)) rom_4 (.addr(counter_1_q), .data(rom_4_data));
  Clock clock_2 (.out(clock_2_out));
  Clock clock_3 (.out(clock_3_out));
  PLEX plex_1 (
    .in_1(rom_2_data), .out_2(plex_1_out_2), .out_3(plex_1_out_3), .out_4(plex_1_out_4));  // open: out_5, out_6, out_7, out_8, out_9, out_10
  Register #(.width(16)) register_1 (
    .D(rom_3_data), .en(plex_1_out_4), .clk(clock_2_out), .Q(register_1_q));  // open: clr
  Register #(.width(16)) register_2 (
    .D(rom_4_data), .en(plex_1_out_4), .clk(clock_3_out), .Q(register_2_q));  // open: clr
  or or_1 (or_1_out, plex_1_out_3, plex_1_out_2, plex_1_out_4);
  assign controlled_buffer_1_out = or_1_out ? adder_1_out : 16'bz;  // Controlled_Buffer controlled_buffer_1
  not not_1 (not_1_out, or_1_out);
  assign controlled_buffer_1_out = not_1_out ? {16{1'b0}} : 16'bz;  // Controlled_Buffer controlled_buffer_2
  RAM #(.addrWidth(16), .dataWidth(16)) ram_1 (
    .addr(register_2_q), .we(1'b1), .oe(1'b1), .clk(clock_4_out), .din(controlled_buffer_1_out),
    .dout(ram_1_dout));
  Clock clock_4 (.out(clock_4_out));
  Adder #(.width(16)) adder_1 (.a(register_1_q), .b(ram_1_dout), .out(adder_1_out));  // open: cin, cout

  // Notes on the sheet:
  //   contents of rom_2 (hex, n*v repeats v):
  //   4*2 3 0 0 0 1
  //   contents of rom_3 (hex, n*v repeats v):
  //   1 1 1
  //   contents of rom_4 (hex, n*v repeats v):
  //   8*1
endmodule

module PC120 (
);

  wire clock_1_out, clock_2_out, clock_3_out, clock_4_out, comparator_1_gt, controlled_buffer_1_out,
       not_1_out, or_1_out, plex_1_out_2, plex_1_out_3, plex_1_out_4;
  wire [15:0] adder_1_out, controlled_buffer_2_out, counter_1_q, ram_1_dout, register_1_q, register_2_q,
       rom_1_data, rom_2_data, rom_3_data, rom_4_data, rom_5_data;

  Clock clock_1 (.out(clock_1_out));
  ROM #(.addrWidth(16), .dataWidth(16)) rom_1 (.addr(counter_1_q), .data(rom_1_data));
  Counter #(.max('hffff), .width(16)) counter_1 (
    .load(controlled_buffer_1_out), .clk(clock_1_out), .D(rom_1_data), .Q(counter_1_q));  // open: clr, up, count, carry
  ROM #(.addrWidth(16), .dataWidth(16)) rom_2 (.addr(counter_1_q), .data(rom_2_data));
  ROM #(.addrWidth(16), .dataWidth(16)) rom_3 (.addr(counter_1_q), .data(rom_3_data));
  ROM #(.addrWidth(16), .dataWidth(16)) rom_4 (.addr(counter_1_q), .data(rom_4_data));
  Clock clock_2 (.out(clock_2_out));
  Clock clock_3 (.out(clock_3_out));
  assign controlled_buffer_1_out = plex_1_out_3 ? comparator_1_gt : 1'bz;  // Controlled_Buffer controlled_buffer_1
  PLEX plex_1 (
    .in_1(rom_3_data), .out_2(plex_1_out_2), .out_3(plex_1_out_3), .out_4(plex_1_out_4));  // open: out_5, out_6, out_7, out_8, out_9, out_10
  Register #(.width(16)) register_1 (
    .D(rom_2_data), .en(plex_1_out_4), .clk(clock_2_out), .Q(register_1_q));  // open: clr
  Register #(.width(16)) register_2 (
    .D(rom_4_data), .en(plex_1_out_4), .clk(clock_3_out), .Q(register_2_q));  // open: clr
  ROM #(.addrWidth(16), .dataWidth(16)) rom_5 (.addr(counter_1_q), .data(rom_5_data));
  assign controlled_buffer_2_out = or_1_out ? adder_1_out : 16'bz;  // Controlled_Buffer controlled_buffer_2
  or or_1 (or_1_out, plex_1_out_3, plex_1_out_2, plex_1_out_4);
  assign controlled_buffer_2_out = not_1_out ? {16{1'b0}} : 16'bz;  // Controlled_Buffer controlled_buffer_3
  not not_1 (not_1_out, or_1_out);
  Clock clock_4 (.out(clock_4_out));
  RAM #(.addrWidth(16), .dataWidth(16)) ram_1 (
    .addr(register_2_q), .we(1'b1), .oe(1'b1), .clk(clock_4_out), .din(controlled_buffer_2_out),
    .dout(ram_1_dout));
  Comparator #(.width(16)) comparator_1 (.a(rom_5_data), .b(adder_1_out), .gt(comparator_1_gt));  // open: eq, lt
  Adder #(.width(16)) adder_1 (.a(register_1_q), .b(ram_1_dout), .out(adder_1_out));  // open: cin, cout

  // Notes on the sheet:
  //   contents of rom_2 (hex, n*v repeats v):
  //   1 1 1
  //   contents of rom_3 (hex, n*v repeats v):
  //   4*2 3 0 0 0 1
  //   contents of rom_4 (hex, n*v repeats v):
  //   8*1
  //   contents of rom_5 (hex, n*v repeats v):
  //   6*0 1 1 ffff
endmodule

module PC200 (
);

  wire clock_1_out, clock_2_out, clock_3_out, clock_4_out, not_1_out, or_1_out, plex_1_out_2, plex_1_out_3,
       plex_1_out_4;
  wire [15:0] adder_1_out, controlled_buffer_1_out, counter_1_q, ram_1_dout, register_1_q, register_2_q,
       rom_1_data, rom_2_data, rom_3_data, rom_4_data;

  ROM #(.addrWidth(16), .dataWidth(16)) rom_1 (.addr(counter_1_q), .data(rom_1_data));
  Counter #(.max('hffff), .width(16)) counter_1 (
    .load(plex_1_out_3), .clk(clock_1_out), .D(rom_1_data), .Q(counter_1_q));  // open: clr, up, count, carry
  Clock clock_1 (.out(clock_1_out));
  ROM #(.addrWidth(16), .dataWidth(16)) rom_2 (.addr(counter_1_q), .data(rom_2_data));
  ROM #(.addrWidth(16), .dataWidth(16)) rom_3 (.addr(counter_1_q), .data(rom_3_data));
  ROM #(.addrWidth(16), .dataWidth(16)) rom_4 (.addr(counter_1_q), .data(rom_4_data));
  Clock clock_2 (.out(clock_2_out));
  Clock clock_3 (.out(clock_3_out));
  PLEX plex_1 (
    .in_1(rom_2_data), .out_2(plex_1_out_2), .out_3(plex_1_out_3), .out_4(plex_1_out_4));  // open: out_5, out_6, out_7, out_8, out_9, out_10
  Register #(.width(16)) register_1 (
    .D(rom_3_data), .en(plex_1_out_4), .clk(clock_2_out), .Q(register_1_q));  // open: clr
  Register #(.width(16)) register_2 (
    .D(rom_4_data), .en(plex_1_out_4), .clk(clock_3_out), .Q(register_2_q));  // open: clr
  assign controlled_buffer_1_out = or_1_out ? adder_1_out : 16'bz;  // Controlled_Buffer controlled_buffer_1
  or or_1 (or_1_out, plex_1_out_3, plex_1_out_2, plex_1_out_4);
  not not_1 (not_1_out, or_1_out);
  Clock clock_4 (.out(clock_4_out));
  assign controlled_buffer_1_out = not_1_out ? {16{1'b0}} : 16'bz;  // Controlled_Buffer controlled_buffer_2
  RAM #(.addrWidth(16), .dataWidth(16)) ram_1 (
    .addr(register_2_q), .we(1'b1), .oe(1'b1), .clk(clock_4_out), .din(controlled_buffer_1_out),
    .dout(ram_1_dout));
  Adder #(.width(16)) adder_1 (.a(register_1_q), .b(ram_1_dout), .out(adder_1_out));  // open: cin, cout

  // Notes on the sheet:
  //   contents of rom_2 (hex, n*v repeats v):
  //   4*2 3 0 0 0 1
  //   contents of rom_3 (hex, n*v repeats v):
  //   1 1 1
  //   contents of rom_4 (hex, n*v repeats v):
  //   8*1
endmodule

module PC205 (
);

  wire clock_1_out, clock_2_out, clock_3_out, clock_4_out, not_1_out, or_1_out, plex_1_out_2, plex_1_out_3,
       plex_1_out_4;
  wire [15:0] adder_1_out, controlled_buffer_1_out, counter_1_q, ram_1_dout, register_1_q, register_2_q,
       rom_1_data, rom_2_data, rom_3_data, rom_4_data;

  ROM #(.addrWidth(16), .dataWidth(16)) rom_1 (.addr(counter_1_q), .data(rom_1_data));
  Counter #(.max('hffff), .width(16)) counter_1 (
    .load(plex_1_out_3), .clk(clock_1_out), .D(rom_1_data), .Q(counter_1_q));  // open: clr, up, count, carry
  Clock clock_1 (.out(clock_1_out));
  ROM #(.addrWidth(16), .dataWidth(16)) rom_2 (.addr(counter_1_q), .data(rom_2_data));
  ROM #(.addrWidth(16), .dataWidth(16)) rom_3 (.addr(counter_1_q), .data(rom_3_data));
  ROM #(.addrWidth(16), .dataWidth(16)) rom_4 (.addr(counter_1_q), .data(rom_4_data));
  Clock clock_2 (.out(clock_2_out));
  Clock clock_3 (.out(clock_3_out));
  PLEX plex_1 (
    .in_1(rom_2_data), .out_2(plex_1_out_2), .out_3(plex_1_out_3), .out_4(plex_1_out_4));  // open: out_5, out_6, out_7, out_8, out_9, out_10
  Register #(.width(16)) register_1 (
    .D(rom_3_data), .en(plex_1_out_4), .clk(clock_2_out), .Q(register_1_q));  // open: clr
  Register #(.width(16)) register_2 (
    .D(rom_4_data), .en(plex_1_out_4), .clk(clock_3_out), .Q(register_2_q));  // open: clr
  or or_1 (or_1_out, plex_1_out_3, plex_1_out_2, plex_1_out_4);
  assign controlled_buffer_1_out = or_1_out ? adder_1_out : 16'bz;  // Controlled_Buffer controlled_buffer_1
  not not_1 (not_1_out, or_1_out);
  assign controlled_buffer_1_out = not_1_out ? {16{1'b0}} : 16'bz;  // Controlled_Buffer controlled_buffer_2
  RAM #(.addrWidth(16), .dataWidth(16)) ram_1 (
    .addr(register_2_q), .we(1'b1), .oe(1'b1), .clk(clock_4_out), .din(controlled_buffer_1_out),
    .dout(ram_1_dout));
  Clock clock_4 (.out(clock_4_out));
  Adder #(.width(16)) adder_1 (.a(register_1_q), .b(ram_1_dout), .out(adder_1_out));  // open: cin, cout

  // Notes on the sheet:
  //   contents of rom_2 (hex, n*v repeats v):
  //   4*2 3 0 0 0 1
  //   contents of rom_3 (hex, n*v repeats v):
  //   1 1 1
  //   contents of rom_4 (hex, n*v repeats v):
  //   8*1
endmodule

module PC210 (
);

  wire clock_1_out, clock_2_out, clock_3_out, clock_4_out, not_1_out, or_1_out, plexv2_1_out_2,
       plexv2_1_out_3, plexv2_1_out_4;
  wire [15:0] adder_1_out, controlled_buffer_1_out, counter_1_q, ram_1_dout, register_1_q, register_2_q,
       rom_1_data, rom_2_data, rom_3_data, rom_4_data;

  Clock clock_1 (.out(clock_1_out));
  ROM #(.addrWidth(16), .dataWidth(16)) rom_1 (.addr(counter_1_q), .data(rom_1_data));
  Counter #(.max('hffff), .width(16)) counter_1 (
    .load(plexv2_1_out_3), .clk(clock_1_out), .D(rom_1_data), .Q(counter_1_q));  // open: clr, up, count, carry
  ROM #(.addrWidth(16), .dataWidth(16)) rom_2 (.addr(counter_1_q), .data(rom_2_data));
  ROM #(.addrWidth(16), .dataWidth(16)) rom_3 (.addr(counter_1_q), .data(rom_3_data));
  ROM #(.addrWidth(16), .dataWidth(16)) rom_4 (.addr(counter_1_q), .data(rom_4_data));
  Register #(.width(16)) register_1 (
    .D(rom_2_data), .en(plexv2_1_out_4), .clk(clock_2_out), .Q(register_1_q));  // open: clr
  Clock clock_2 (.out(clock_2_out));
  Register #(.width(16)) register_2 (
    .D(rom_4_data), .en(plexv2_1_out_4), .clk(clock_3_out), .Q(register_2_q));  // open: clr
  Clock clock_3 (.out(clock_3_out));
  PLEXv2 plexv2_1 (
    .in_1(rom_3_data), .out_2(plexv2_1_out_2), .out_3(plexv2_1_out_3), .out_4(plexv2_1_out_4));  // open: out_5
  assign controlled_buffer_1_out = or_1_out ? adder_1_out : 16'bz;  // Controlled_Buffer controlled_buffer_1
  or or_1 (or_1_out, plexv2_1_out_3, plexv2_1_out_2, plexv2_1_out_4);
  assign controlled_buffer_1_out = not_1_out ? {16{1'b0}} : 16'bz;  // Controlled_Buffer controlled_buffer_2
  not not_1 (not_1_out, or_1_out);
  Clock clock_4 (.out(clock_4_out));
  RAM #(.addrWidth(16), .dataWidth(16)) ram_1 (
    .addr(register_2_q), .we(1'b1), .oe(1'b1), .clk(clock_4_out), .din(controlled_buffer_1_out),
    .dout(ram_1_dout));
  Adder #(.width(16)) adder_1 (.a(register_1_q), .b(ram_1_dout), .out(adder_1_out));  // open: cin, cout

  // Notes on the sheet:
  //   contents of rom_2 (hex, n*v repeats v):
  //   1 1 1
  //   contents of rom_3 (hex, n*v repeats v):
  //   4*2 3 0 0 0 1
  //   contents of rom_4 (hex, n*v repeats v):
  //   8*1
endmodule

// PLEX
module PLEXv2 (
  input  [15:0] in_1,
  output out_2,
  output out_3,
  output out_4,
  output out_5
);

  Comparator #(.width(16)) comparator_1 (.a(in_1), .b({16{1'b0}}), .eq(out_2));  // open: gt, lt
  Comparator #(.width(16)) comparator_2 (.a(in_1), .b(16'h1), .eq(out_3));  // open: gt, lt
  Comparator #(.width(16)) comparator_3 (.a(in_1), .b(16'h2), .eq(out_4));  // open: gt, lt
  Comparator #(.width(16)) comparator_4 (.a(in_1), .b(16'h3), .eq(out_5));  // open: gt, lt
endmodule

module PC220 (
);

  wire clock_1_out, clock_2_out, clock_3_out, clock_4_out, not_1_out, or_1_out, plex_1_out_2, plex_1_out_3,
       plex_1_out_4;
  wire [15:0] adder_1_out, controlled_buffer_1_out, counter_1_q, ram_1_dout, register_1_q, register_2_q,
       rom_1_data, rom_2_data, rom_3_data, rom_4_data;

  ROM #(.addrWidth(16), .dataWidth(16)) rom_1 (.addr(counter_1_q), .data(rom_1_data));
  Counter #(.max('hffff), .width(16)) counter_1 (
    .load(plex_1_out_3), .clk(clock_1_out), .D(rom_1_data), .Q(counter_1_q));  // open: clr, up, count, carry
  Clock clock_1 (.out(clock_1_out));
  ROM #(.addrWidth(16), .dataWidth(16)) rom_2 (.addr(counter_1_q), .data(rom_2_data));
  ROM #(.addrWidth(16), .dataWidth(16)) rom_3 (.addr(counter_1_q), .data(rom_3_data));
  ROM #(.addrWidth(16), .dataWidth(16)) rom_4 (.addr(counter_1_q), .data(rom_4_data));
  Clock clock_2 (.out(clock_2_out));
  Clock clock_3 (.out(clock_3_out));
  PLEX plex_1 (
    .in_1(rom_2_data), .out_2(plex_1_out_2), .out_3(plex_1_out_3), .out_4(plex_1_out_4));  // open: out_5, out_6, out_7, out_8, out_9, out_10
  Register #(.width(16)) register_1 (
    .D(rom_3_data), .en(plex_1_out_4), .clk(clock_2_out), .Q(register_1_q));  // open: clr
  Register #(.width(16)) register_2 (
    .D(rom_4_data), .en(plex_1_out_4), .clk(clock_3_out), .Q(register_2_q));  // open: clr
  or or_1 (or_1_out, plex_1_out_3, plex_1_out_2, plex_1_out_4);
  assign controlled_buffer_1_out = or_1_out ? adder_1_out : 16'bz;  // Controlled_Buffer controlled_buffer_1
  not not_1 (not_1_out, or_1_out);
  assign controlled_buffer_1_out = not_1_out ? {16{1'b0}} : 16'bz;  // Controlled_Buffer controlled_buffer_2
  RAM #(.addrWidth(16), .dataWidth(16)) ram_1 (
    .addr(register_2_q), .we(1'b1), .oe(1'b1), .clk(clock_4_out), .din(controlled_buffer_1_out),
    .dout(ram_1_dout));
  Clock clock_4 (.out(clock_4_out));
  Adder #(.width(16)) adder_1 (.a(register_1_q), .b(ram_1_dout), .out(adder_1_out));  // open: cin, cout

  // Notes on the sheet:
  //   contents of rom_2 (hex, n*v repeats v):
  //   4*2 3 0 0 0 1
  //   contents of rom_3 (hex, n*v repeats v):
  //   1 1 1
  //   contents of rom_4 (hex, n*v repeats v):
  //   8*1
endmodule

module PC225 (
);

  wire clock_1_out, clock_2_out, clock_3_out, clock_4_out, not_1_out, or_1_out, or_2_out, or_3_out,
       plex_1_out_2, plex_1_out_3, plex_1_out_4, plex_1_out_6, plex_1_out_7, plex_1_out_8, plex_1_out_9;
  wire [15:0] adder_1_out, controlled_buffer_1_out, counter_1_q, ram_1_dout, register_1_q, register_2_q,
       rom_1_data, rom_2_data, rom_3_data, rom_4_data;

  Clock clock_1 (.out(clock_1_out));
  ROM #(.addrWidth(16), .dataWidth(16)) rom_1 (.addr(counter_1_q), .data(rom_1_data));
  Counter #(.max('hffff), .width(16)) counter_1 (
    .load(plex_1_out_3), .clk(clock_1_out), .D(rom_1_data), .Q(counter_1_q));  // open: clr, up, count, carry
  ROM #(.addrWidth(16), .dataWidth(16)) rom_2 (.addr(counter_1_q), .data(rom_2_data));
  ROM #(.addrWidth(16), .dataWidth(16)) rom_3 (.addr(counter_1_q), .data(rom_3_data));
  ROM #(.addrWidth(16), .dataWidth(16)) rom_4 (.addr(counter_1_q), .data(rom_4_data));
  Register #(.width(16)) register_1 (
    .D(rom_2_data), .en(plex_1_out_4), .clk(clock_2_out), .Q(register_1_q));  // open: clr
  Clock clock_2 (.out(clock_2_out));
  Register #(.width(16)) register_2 (
    .D(rom_4_data), .en(plex_1_out_4), .clk(clock_3_out), .Q(register_2_q));  // open: clr
  Clock clock_3 (.out(clock_3_out));
  PLEX plex_1 (
    .in_1(rom_3_data), .out_2(plex_1_out_2), .out_3(plex_1_out_3), .out_4(plex_1_out_4),
    .out_6(plex_1_out_6), .out_7(plex_1_out_7), .out_8(plex_1_out_8), .out_9(plex_1_out_9));  // open: out_5, out_10
  or or_1 (or_1_out, plex_1_out_6, plex_1_out_7, plex_1_out_8, plex_1_out_9);
  or or_2 (or_2_out, plex_1_out_3, plex_1_out_2, plex_1_out_4);
  or or_3 (or_3_out, or_2_out, or_1_out);
  assign controlled_buffer_1_out = or_3_out ? adder_1_out : 16'bz;  // Controlled_Buffer controlled_buffer_1
  not not_1 (not_1_out, or_3_out);
  assign controlled_buffer_1_out = not_1_out ? {16{1'b0}} : 16'bz;  // Controlled_Buffer controlled_buffer_2
  RAM #(.addrWidth(16), .dataWidth(16)) ram_1 (
    .addr(register_2_q), .we(1'b1), .oe(1'b1), .clk(clock_4_out), .din(controlled_buffer_1_out),
    .dout(ram_1_dout));
  Clock clock_4 (.out(clock_4_out));
  Adder #(.width(16)) adder_1 (.a(register_1_q), .b(ram_1_dout), .out(adder_1_out));  // open: cin, cout

  // Notes on the sheet:
  //   contents of rom_2 (hex, n*v repeats v):
  //   1 1 1
  //   contents of rom_3 (hex, n*v repeats v):
  //   4*2 3 0 0 0 1
  //   contents of rom_4 (hex, n*v repeats v):
  //   8*1
endmodule

module PC240 (
);

  wire clock_1_out, clock_2_out, clock_3_out, clock_4_out, not_1_out, or_1_out, or_2_out, or_3_out,
       plex_1_out_2, plex_1_out_3, plex_1_out_4, plex_1_out_6, plex_1_out_7, plex_1_out_8, plex_1_out_9;
  wire [15:0] adder_1_out, controlled_buffer_1_out, counter_1_q, ram_1_dout, register_1_q, register_2_q,
       rom_1_data, rom_2_data, rom_3_data, rom_4_data;

  ROM #(.addrWidth(16), .dataWidth(16)) rom_1 (.addr(counter_1_q), .data(rom_1_data));
  Counter #(.max('hffff), .width(16)) counter_1 (
    .load(plex_1_out_3), .clk(clock_1_out), .D(rom_1_data), .Q(counter_1_q));  // open: clr, up, count, carry
  Clock clock_1 (.out(clock_1_out));
  ROM #(.addrWidth(16), .dataWidth(16)) rom_2 (.addr(counter_1_q), .data(rom_2_data));
  ROM #(.addrWidth(16), .dataWidth(16)) rom_3 (.addr(counter_1_q), .data(rom_3_data));
  ROM #(.addrWidth(16), .dataWidth(16)) rom_4 (.addr(counter_1_q), .data(rom_4_data));
  Clock clock_2 (.out(clock_2_out));
  Clock clock_3 (.out(clock_3_out));
  PLEX plex_1 (
    .in_1(rom_2_data), .out_2(plex_1_out_2), .out_3(plex_1_out_3), .out_4(plex_1_out_4),
    .out_6(plex_1_out_6), .out_7(plex_1_out_7), .out_8(plex_1_out_8), .out_9(plex_1_out_9));  // open: out_5, out_10
  Register #(.width(16)) register_1 (
    .D(rom_3_data), .en(plex_1_out_4), .clk(clock_2_out), .Q(register_1_q));  // open: clr
  Register #(.width(16)) register_2 (
    .D(rom_4_data), .en(plex_1_out_4), .clk(clock_3_out), .Q(register_2_q));  // open: clr
  or or_1 (or_1_out, plex_1_out_6, plex_1_out_7, plex_1_out_8, plex_1_out_9);
  or or_2 (or_2_out, plex_1_out_3, plex_1_out_2, plex_1_out_4);
  or or_3 (or_3_out, or_2_out, or_1_out);
  assign controlled_buffer_1_out = or_3_out ? adder_1_out : 16'bz;  // Controlled_Buffer controlled_buffer_1
  not not_1 (not_1_out, or_3_out);
  assign controlled_buffer_1_out = not_1_out ? {16{1'b0}} : 16'bz;  // Controlled_Buffer controlled_buffer_2
  RAM #(.addrWidth(16), .dataWidth(16)) ram_1 (
    .addr(register_2_q), .we(1'b1), .oe(1'b1), .clk(clock_4_out), .din(controlled_buffer_1_out),
    .dout(ram_1_dout));
  Clock clock_4 (.out(clock_4_out));
  Adder #(.width(16)) adder_1 (.a(register_1_q), .b(ram_1_dout), .out(adder_1_out));  // open: cin, cout

  // Notes on the sheet:
  //   contents of rom_2 (hex, n*v repeats v):
  //   4*2 3 0 0 0 1
  //   contents of rom_3 (hex, n*v repeats v):
  //   1 1 1
  //   contents of rom_4 (hex, n*v repeats v):
  //   8*1
endmodule

module PC245 (
);

  wire clock_1_out, clock_2_out, clock_3_out, clock_4_out, not_1_out, or_1_out, or_2_out, or_3_out,
       plex_1_out_2, plex_1_out_3, plex_1_out_4, plex_1_out_6, plex_1_out_7, plex_1_out_8, plex_1_out_9;
  wire [15:0] adder_1_out, controlled_buffer_1_out, counter_1_q, ram_1_dout, register_1_q, register_2_q,
       rom_1_data, rom_2_data, rom_3_data, rom_4_data;

  ROM #(.addrWidth(16), .dataWidth(16)) rom_1 (.addr(counter_1_q), .data(rom_1_data));
  Counter #(.max('hffff), .width(16)) counter_1 (
    .load(plex_1_out_3), .clk(clock_1_out), .D(rom_1_data), .Q(counter_1_q));  // open: clr, up, count, carry
  Clock clock_1 (.out(clock_1_out));
  ROM #(.addrWidth(16), .dataWidth(16)) rom_2 (.addr(counter_1_q), .data(rom_2_data));
  ROM #(.addrWidth(16), .dataWidth(16)) rom_3 (.addr(counter_1_q), .data(rom_3_data));
  ROM #(.addrWidth(16), .dataWidth(16)) rom_4 (.addr(counter_1_q), .data(rom_4_data));
  Clock clock_2 (.out(clock_2_out));
  Clock clock_3 (.out(clock_3_out));
  PLEX plex_1 (
    .in_1(rom_2_data), .out_2(plex_1_out_2), .out_3(plex_1_out_3), .out_4(plex_1_out_4),
    .out_6(plex_1_out_6), .out_7(plex_1_out_7), .out_8(plex_1_out_8), .out_9(plex_1_out_9));  // open: out_5, out_10
  Register #(.width(16)) register_1 (
    .D(rom_3_data), .en(plex_1_out_4), .clk(clock_2_out), .Q(register_1_q));  // open: clr
  Register #(.width(16)) register_2 (
    .D(rom_4_data), .en(plex_1_out_4), .clk(clock_3_out), .Q(register_2_q));  // open: clr
  or or_1 (or_1_out, plex_1_out_6, plex_1_out_7, plex_1_out_8, plex_1_out_9);
  or or_2 (or_2_out, plex_1_out_3, plex_1_out_2, plex_1_out_4);
  or or_3 (or_3_out, or_2_out, or_1_out);
  assign controlled_buffer_1_out = or_3_out ? adder_1_out : 16'bz;  // Controlled_Buffer controlled_buffer_1
  not not_1 (not_1_out, or_3_out);
  assign controlled_buffer_1_out = not_1_out ? {16{1'b0}} : 16'bz;  // Controlled_Buffer controlled_buffer_2
  RAM #(.addrWidth(16), .dataWidth(16)) ram_1 (
    .addr(register_2_q), .we(1'b1), .oe(1'b1), .clk(clock_4_out), .din(controlled_buffer_1_out),
    .dout(ram_1_dout));
  Clock clock_4 (.out(clock_4_out));
  Adder #(.width(16)) adder_1 (.a(register_1_q), .b(ram_1_dout), .out(adder_1_out));  // open: cin, cout

  // Notes on the sheet:
  //   contents of rom_2 (hex, n*v repeats v):
  //   4*2 3 0 0 0 1
  //   contents of rom_3 (hex, n*v repeats v):
  //   1 1 1
  //   contents of rom_4 (hex, n*v repeats v):
  //   8*1
endmodule

module PC250 (
);

  wire clock_1_out, clock_2_out, clock_3_out, clock_4_out, not_1_out, or_1_out, or_2_out, or_3_out,
       plex_1_out_2, plex_1_out_3, plex_1_out_4, plex_1_out_6, plex_1_out_7, plex_1_out_8, plex_1_out_9;
  wire [15:0] adder_1_out, controlled_buffer_1_out, counter_1_q, ram_1_dout, register_1_q, register_2_q,
       rom_1_data, rom_2_data, rom_3_data, rom_4_data;

  ROM #(.addrWidth(16), .dataWidth(16)) rom_1 (.addr(counter_1_q), .data(rom_1_data));
  Counter #(.max('hffff), .width(16)) counter_1 (
    .load(plex_1_out_3), .clk(clock_1_out), .D(rom_1_data), .Q(counter_1_q));  // open: clr, up, count, carry
  Clock clock_1 (.out(clock_1_out));
  ROM #(.addrWidth(16), .dataWidth(16)) rom_2 (.addr(counter_1_q), .data(rom_2_data));
  ROM #(.addrWidth(16), .dataWidth(16)) rom_3 (.addr(counter_1_q), .data(rom_3_data));
  ROM #(.addrWidth(16), .dataWidth(16)) rom_4 (.addr(counter_1_q), .data(rom_4_data));
  Clock clock_2 (.out(clock_2_out));
  Clock clock_3 (.out(clock_3_out));
  PLEX plex_1 (
    .in_1(rom_2_data), .out_2(plex_1_out_2), .out_3(plex_1_out_3), .out_4(plex_1_out_4),
    .out_6(plex_1_out_6), .out_7(plex_1_out_7), .out_8(plex_1_out_8), .out_9(plex_1_out_9));  // open: out_5, out_10
  Register #(.width(16)) register_1 (
    .D(rom_3_data), .en(plex_1_out_4), .clk(clock_2_out), .Q(register_1_q));  // open: clr
  Register #(.width(16)) register_2 (
    .D(rom_4_data), .en(plex_1_out_4), .clk(clock_3_out), .Q(register_2_q));  // open: clr
  or or_1 (or_1_out, plex_1_out_6, plex_1_out_7, plex_1_out_8, plex_1_out_9);
  or or_2 (or_2_out, plex_1_out_3, plex_1_out_2, plex_1_out_4);
  or or_3 (or_3_out, or_2_out, or_1_out);
  assign controlled_buffer_1_out = or_3_out ? adder_1_out : 16'bz;  // Controlled_Buffer controlled_buffer_1
  not not_1 (not_1_out, or_3_out);
  assign controlled_buffer_1_out = not_1_out ? {16{1'b0}} : 16'bz;  // Controlled_Buffer controlled_buffer_2
  RAM #(.addrWidth(16), .dataWidth(16)) ram_1 (
    .addr(register_2_q), .we(1'b1), .oe(1'b1), .clk(clock_4_out), .din(controlled_buffer_1_out),
    .dout(ram_1_dout));
  Clock clock_4 (.out(clock_4_out));
  Adder #(.width(16)) adder_1 (.a(register_1_q), .b(ram_1_dout), .out(adder_1_out));  // open: cin, cout

  // Notes on the sheet:
  //   contents of rom_2 (hex, n*v repeats v):
  //   4*2 3 0 0 0 1
  //   contents of rom_3 (hex, n*v repeats v):
  //   1 1 1
  //   contents of rom_4 (hex, n*v repeats v):
  //   8*1
endmodule

module PC255 (
);

  wire clock_1_out, clock_2_out, clock_3_out, clock_4_out, not_1_out, or_1_p5, or_2_out, or_3_out,
       plex_1_out_2, plex_1_out_3, plex_1_out_4, plex_1_out_6, plex_1_out_7, plex_1_out_8, plex_1_out_9;
  wire [15:0] adder_1_out, controlled_buffer_1_out, counter_1_q, ram_1_dout, register_1_q, register_2_q,
       rom_1_data, rom_2_data, rom_3_data, rom_4_data;

  Clock clock_1 (.out(clock_1_out));
  ROM #(.addrWidth(16), .dataWidth(16)) rom_1 (.addr(counter_1_q), .data(rom_1_data));
  Counter #(.max('hffff), .width(16)) counter_1 (
    .load(plex_1_out_3), .clk(clock_1_out), .D(rom_1_data), .Q(counter_1_q));  // open: clr, up, count, carry
  ROM #(.addrWidth(16), .dataWidth(16)) rom_2 (.addr(counter_1_q), .data(rom_2_data));
  ROM #(.addrWidth(16), .dataWidth(16)) rom_3 (.addr(counter_1_q), .data(rom_3_data));
  ROM #(.addrWidth(16), .dataWidth(16)) rom_4 (.addr(counter_1_q), .data(rom_4_data));
  Register #(.width(16)) register_1 (
    .D(rom_2_data), .en(plex_1_out_4), .clk(clock_2_out), .Q(register_1_q));  // open: clr
  Clock clock_2 (.out(clock_2_out));
  Register #(.width(16)) register_2 (
    .D(rom_4_data), .en(plex_1_out_4), .clk(clock_3_out), .Q(register_2_q));  // open: clr
  Clock clock_3 (.out(clock_3_out));
  PLEX plex_1 (
    .in_1(rom_3_data), .out_2(plex_1_out_2), .out_3(plex_1_out_3), .out_4(plex_1_out_4),
    .out_6(plex_1_out_6), .out_7(plex_1_out_7), .out_8(plex_1_out_8), .out_9(plex_1_out_9));  // open: out_5, out_10
  // OR_Gate or_1: pin names not known; wires that end beside it: plex_1_out_6, plex_1_out_7, plex_1_out_8, plex_1_out_9, or_1_p5
  or or_2 (or_2_out, plex_1_out_3, plex_1_out_2, plex_1_out_4);
  or or_3 (or_3_out, or_2_out, or_1_p5);
  assign controlled_buffer_1_out = or_3_out ? adder_1_out : 16'bz;  // Controlled_Buffer controlled_buffer_1
  not not_1 (not_1_out, or_3_out);
  assign controlled_buffer_1_out = not_1_out ? {16{1'b0}} : 16'bz;  // Controlled_Buffer controlled_buffer_2
  RAM #(.addrWidth(16), .dataWidth(16)) ram_1 (
    .addr(register_2_q), .we(1'b1), .oe(1'b1), .clk(clock_4_out), .din(controlled_buffer_1_out),
    .dout(ram_1_dout));
  Clock clock_4 (.out(clock_4_out));
  Adder #(.width(16)) adder_1 (.a(register_1_q), .b(ram_1_dout), .out(adder_1_out));  // open: cin, cout

  // Notes on the sheet:
  //   contents of rom_2 (hex, n*v repeats v):
  //   1 1 1
  //   contents of rom_3 (hex, n*v repeats v):
  //   4*2 3 0 0 0 1
  //   contents of rom_4 (hex, n*v repeats v):
  //   8*1
endmodule

module PC280 (
);

  wire clock_1_out, clock_2_out, clock_3_out, clock_4_out, not_1_out, or_1_out, or_2_out, or_3_out,
       plex_1_out_2, plex_1_out_3, plex_1_out_4, plex_1_out_6, plex_1_out_7, plex_1_out_8, plex_1_out_9;
  wire [15:0] adder_1_out, controlled_buffer_1_out, counter_1_q, ram_1_dout, register_1_q, register_2_q,
       rom_1_data, rom_2_data, rom_3_data, rom_4_data;

  ROM #(.addrWidth(16), .dataWidth(16)) rom_1 (.addr(counter_1_q), .data(rom_1_data));
  Counter #(.max('hffff), .width(16)) counter_1 (
    .load(plex_1_out_3), .clk(clock_1_out), .D(rom_1_data), .Q(counter_1_q));  // open: clr, up, count, carry
  Clock clock_1 (.out(clock_1_out));
  ROM #(.addrWidth(16), .dataWidth(16)) rom_2 (.addr(counter_1_q), .data(rom_2_data));
  ROM #(.addrWidth(16), .dataWidth(16)) rom_3 (.addr(counter_1_q), .data(rom_3_data));
  ROM #(.addrWidth(16), .dataWidth(16)) rom_4 (.addr(counter_1_q), .data(rom_4_data));
  Clock clock_2 (.out(clock_2_out));
  Clock clock_3 (.out(clock_3_out));
  PLEX plex_1 (
    .in_1(rom_2_data), .out_2(plex_1_out_2), .out_3(plex_1_out_3), .out_4(plex_1_out_4),
    .out_6(plex_1_out_6), .out_7(plex_1_out_7), .out_8(plex_1_out_8), .out_9(plex_1_out_9));  // open: out_5, out_10
  Register #(.width(16)) register_1 (
    .D(rom_3_data), .en(plex_1_out_4), .clk(clock_2_out), .Q(register_1_q));  // open: clr
  Register #(.width(16)) register_2 (
    .D(rom_4_data), .en(plex_1_out_4), .clk(clock_3_out), .Q(register_2_q));  // open: clr
  or or_1 (or_1_out, plex_1_out_6, plex_1_out_7, plex_1_out_8, plex_1_out_9);
  or or_2 (or_2_out, plex_1_out_3, plex_1_out_2, plex_1_out_4);
  assign controlled_buffer_1_out = or_3_out ? adder_1_out : 16'bz;  // Controlled_Buffer controlled_buffer_1
  or or_3 (or_3_out, or_2_out, or_1_out);
  not not_1 (not_1_out, or_3_out);
  Clock clock_4 (.out(clock_4_out));
  assign controlled_buffer_1_out = not_1_out ? {16{1'b0}} : 16'bz;  // Controlled_Buffer controlled_buffer_2
  RAM #(.addrWidth(16), .dataWidth(16)) ram_1 (
    .addr(register_2_q), .we(1'b1), .oe(1'b1), .clk(clock_4_out), .din(controlled_buffer_1_out),
    .dout(ram_1_dout));
  Adder #(.width(16)) adder_1 (.a(register_1_q), .b(ram_1_dout), .out(adder_1_out));  // open: cin, cout

  // Notes on the sheet:
  //   contents of rom_2 (hex, n*v repeats v):
  //   4*2 3 0 0 0 1
  //   contents of rom_3 (hex, n*v repeats v):
  //   1 1 1
  //   contents of rom_4 (hex, n*v repeats v):
  //   8*1
endmodule

module PC300 (
);

  wire clock_1_out, clock_2_out, clock_3_out, clock_4_out, not_1_out, or_1_out, or_2_out, or_3_out,
       plex_1_out_2, plex_1_out_3, plex_1_out_4, plex_1_out_6, plex_1_out_7, plex_1_out_8, plex_1_out_9;
  wire [15:0] adder_1_out, controlled_buffer_1_out, counter_1_q, ram_1_dout, register_1_q, register_2_q,
       rom_1_data, rom_2_data, rom_3_data, rom_4_data;

  Clock clock_1 (.out(clock_1_out));
  ROM #(.addrWidth(16), .dataWidth(16)) rom_1 (.addr(counter_1_q), .data(rom_1_data));
  Counter #(.max('hffff), .width(16)) counter_1 (
    .load(plex_1_out_3), .clk(clock_1_out), .D(rom_1_data), .Q(counter_1_q));  // open: clr, up, count, carry
  ROM #(.addrWidth(16), .dataWidth(16)) rom_2 (.addr(counter_1_q), .data(rom_2_data));
  ROM #(.addrWidth(16), .dataWidth(16)) rom_3 (.addr(counter_1_q), .data(rom_3_data));
  ROM #(.addrWidth(16), .dataWidth(16)) rom_4 (.addr(counter_1_q), .data(rom_4_data));
  Clock clock_2 (.out(clock_2_out));
  Clock clock_3 (.out(clock_3_out));
  PLEX plex_1 (
    .in_1(rom_3_data), .out_2(plex_1_out_2), .out_3(plex_1_out_3), .out_4(plex_1_out_4),
    .out_6(plex_1_out_6), .out_7(plex_1_out_7), .out_8(plex_1_out_8), .out_9(plex_1_out_9));  // open: out_5, out_10
  Register #(.width(16)) register_1 (
    .D(rom_2_data), .en(plex_1_out_4), .clk(clock_2_out), .Q(register_1_q));  // open: clr
  Register #(.width(16)) register_2 (
    .D(rom_4_data), .en(plex_1_out_4), .clk(clock_3_out), .Q(register_2_q));  // open: clr
  or or_1 (or_1_out, plex_1_out_6, plex_1_out_7, plex_1_out_8, plex_1_out_9);
  or or_2 (or_2_out, plex_1_out_3, plex_1_out_2, plex_1_out_4);
  assign controlled_buffer_1_out = or_3_out ? adder_1_out : 16'bz;  // Controlled_Buffer controlled_buffer_1
  or or_3 (or_3_out, or_2_out, or_1_out);
  assign controlled_buffer_1_out = not_1_out ? {16{1'b0}} : 16'bz;  // Controlled_Buffer controlled_buffer_2
  not not_1 (not_1_out, or_3_out);
  Clock clock_4 (.out(clock_4_out));
  RAM #(.addrWidth(16), .dataWidth(16)) ram_1 (
    .addr(register_2_q), .we(1'b1), .oe(1'b1), .clk(clock_4_out), .din(controlled_buffer_1_out),
    .dout(ram_1_dout));
  Adder #(.width(16)) adder_1 (.a(register_1_q), .b(ram_1_dout), .out(adder_1_out));  // open: cin, cout

  // Notes on the sheet:
  //   contents of rom_2 (hex, n*v repeats v):
  //   1 1 1
  //   contents of rom_3 (hex, n*v repeats v):
  //   4*2 3 0 0 0 1
  //   contents of rom_4 (hex, n*v repeats v):
  //   8*1
endmodule

module PC305 (
);

  wire clock_1_out, clock_2_out, clock_3_out, clock_4_out, not_1_out, or_1_out, or_2_out, or_3_out,
       plex_1_out_2, plex_1_out_3, plex_1_out_4, plex_1_out_6, plex_1_out_7, plex_1_out_8, plex_1_out_9;
  wire [15:0] adder_1_out, controlled_buffer_1_out, counter_1_q, ram_1_dout, register_1_q, register_2_q,
       rom_1_data, rom_2_data, rom_3_data, rom_4_data;

  Clock clock_1 (.out(clock_1_out));
  ROM #(.addrWidth(16), .dataWidth(16)) rom_1 (.addr(counter_1_q), .data(rom_1_data));
  Counter #(.max('hffff), .width(16)) counter_1 (
    .load(plex_1_out_3), .clk(clock_1_out), .D(rom_1_data), .Q(counter_1_q));  // open: clr, up, count, carry
  ROM #(.addrWidth(16), .dataWidth(16)) rom_2 (.addr(counter_1_q), .data(rom_2_data));
  ROM #(.addrWidth(16), .dataWidth(16)) rom_3 (.addr(counter_1_q), .data(rom_3_data));
  ROM #(.addrWidth(16), .dataWidth(16)) rom_4 (.addr(counter_1_q), .data(rom_4_data));
  Register #(.width(16)) register_1 (
    .D(rom_2_data), .en(plex_1_out_4), .clk(clock_2_out), .Q(register_1_q));  // open: clr
  Clock clock_2 (.out(clock_2_out));
  Register #(.width(16)) register_2 (
    .D(rom_4_data), .en(plex_1_out_4), .clk(clock_3_out), .Q(register_2_q));  // open: clr
  Clock clock_3 (.out(clock_3_out));
  PLEX plex_1 (
    .in_1(rom_3_data), .out_2(plex_1_out_2), .out_3(plex_1_out_3), .out_4(plex_1_out_4),
    .out_6(plex_1_out_6), .out_7(plex_1_out_7), .out_8(plex_1_out_8), .out_9(plex_1_out_9));  // open: out_5, out_10
  or or_1 (or_1_out, plex_1_out_6, plex_1_out_7, plex_1_out_8, plex_1_out_9);
  or or_2 (or_2_out, plex_1_out_3, plex_1_out_2, plex_1_out_4);
  or or_3 (or_3_out, or_2_out, or_1_out);
  assign controlled_buffer_1_out = or_3_out ? adder_1_out : 16'bz;  // Controlled_Buffer controlled_buffer_1
  not not_1 (not_1_out, or_3_out);
  assign controlled_buffer_1_out = not_1_out ? {16{1'b0}} : 16'bz;  // Controlled_Buffer controlled_buffer_2
  RAM #(.addrWidth(16), .dataWidth(16)) ram_1 (
    .addr(register_2_q), .we(1'b1), .oe(1'b1), .clk(clock_4_out), .din(controlled_buffer_1_out),
    .dout(ram_1_dout));
  Clock clock_4 (.out(clock_4_out));
  Adder #(.width(16)) adder_1 (.a(register_1_q), .b(ram_1_dout), .out(adder_1_out));  // open: cin, cout

  // Notes on the sheet:
  //   contents of rom_2 (hex, n*v repeats v):
  //   1 1 1
  //   contents of rom_3 (hex, n*v repeats v):
  //   4*2 3 0 0 0 1
  //   contents of rom_4 (hex, n*v repeats v):
  //   8*1
endmodule

module PC310 (
);

  wire clock_1_out, clock_2_out, clock_3_out, clock_4_out, comparator_1_gt, comparator_1_lt, not_1_out,
       or_1_out, or_2_out, or_3_out, plex_1_out_2, plex_1_out_3, plex_1_out_4, plex_1_out_6, plex_1_out_7,
       plex_1_out_8, plex_1_out_9;
  wire [15:0] adder_1_out, controlled_buffer_1_out, counter_1_q, ram_1_dout, register_1_q, register_2_q,
       rom_1_data, rom_2_data, rom_3_data, rom_4_data, rom_5_data;

  Clock clock_1 (.out(clock_1_out));
  ROM #(.addrWidth(16), .dataWidth(16)) rom_1 (.addr(counter_1_q), .data(rom_1_data));
  Counter #(.max('hffff), .width(16)) counter_1 (
    .load(plex_1_out_3), .clk(clock_1_out), .D(rom_1_data), .Q(counter_1_q));  // open: clr, up, count, carry
  ROM #(.addrWidth(16), .dataWidth(16)) rom_2 (.addr(counter_1_q), .data(rom_2_data));
  ROM #(.addrWidth(16), .dataWidth(16)) rom_3 (.addr(counter_1_q), .data(rom_3_data));
  ROM #(.addrWidth(16), .dataWidth(16)) rom_4 (.addr(counter_1_q), .data(rom_4_data));
  Register #(.width(16)) register_1 (
    .D(rom_2_data), .en(plex_1_out_4), .clk(clock_2_out), .Q(register_1_q));  // open: clr
  Clock clock_2 (.out(clock_2_out));
  Register #(.width(16)) register_2 (
    .D(rom_4_data), .en(plex_1_out_4), .clk(clock_3_out), .Q(register_2_q));  // open: clr
  Clock clock_3 (.out(clock_3_out));
  PLEX plex_1 (
    .in_1(rom_3_data), .out_2(plex_1_out_2), .out_3(plex_1_out_3), .out_4(plex_1_out_4),
    .out_6(plex_1_out_6), .out_7(plex_1_out_7), .out_8(plex_1_out_8), .out_9(plex_1_out_9));  // open: out_5, out_10
  or or_1 (or_1_out, plex_1_out_6, plex_1_out_7, plex_1_out_8, plex_1_out_9);
  or or_2 (or_2_out, plex_1_out_3, plex_1_out_2, plex_1_out_4);
  or or_3 (or_3_out, or_2_out, or_1_out);
  ROM #(.addrWidth(16), .dataWidth(16)) rom_5 (.addr(counter_1_q), .data(rom_5_data));
  assign controlled_buffer_1_out = or_3_out ? adder_1_out : 16'bz;  // Controlled_Buffer controlled_buffer_1
  not not_1 (not_1_out, or_3_out);
  assign controlled_buffer_1_out = not_1_out ? {16{1'b0}} : 16'bz;  // Controlled_Buffer controlled_buffer_2
  RAM #(.addrWidth(16), .dataWidth(16)) ram_1 (
    .addr(register_2_q), .we(1'b1), .oe(1'b1), .clk(clock_4_out), .din(controlled_buffer_1_out),
    .dout(ram_1_dout));
  Clock clock_4 (.out(clock_4_out));
  Adder #(.width(16)) adder_1 (.a(register_1_q), .b(ram_1_dout), .out(adder_1_out));  // open: cin, cout
  Comparator #(.width(16)) comparator_1 (
    .a(rom_5_data), .b(adder_1_out), .gt(comparator_1_gt), .lt(comparator_1_lt));  // open: eq
  LED led_1 (.in(comparator_1_gt));
  LED led_2 (.in(comparator_1_lt));

  // Notes on the sheet:
  //   contents of rom_2 (hex, n*v repeats v):
  //   1 1 1
  //   contents of rom_3 (hex, n*v repeats v):
  //   4*2 3 0 0 0 1
  //   contents of rom_4 (hex, n*v repeats v):
  //   8*1
  //   contents of rom_5 (hex, n*v repeats v):
  //   8*1
endmodule

module PC315 (
);

  wire clock_1_out, clock_2_out, clock_3_out, clock_4_out, comparator_1_gt, comparator_1_lt, not_1_out,
       or_1_out, or_2_out, or_3_out, plex_1_out_2, plex_1_out_3, plex_1_out_4, plex_1_out_6, plex_1_out_7,
       plex_1_out_8, plex_1_out_9;
  wire [15:0] adder_1_out, controlled_buffer_1_out, counter_1_q, ram_1_dout, register_1_q, register_2_q,
       rom_1_data, rom_2_data, rom_3_data, rom_4_data, rom_5_data;

  ROM #(.addrWidth(16), .dataWidth(16)) rom_1 (.addr(counter_1_q), .data(rom_1_data));
  Counter #(.max('hffff), .width(16)) counter_1 (
    .load(plex_1_out_3), .clk(clock_1_out), .D(rom_1_data), .Q(counter_1_q));  // open: clr, up, count, carry
  Clock clock_1 (.out(clock_1_out));
  ROM #(.addrWidth(16), .dataWidth(16)) rom_2 (.addr(counter_1_q), .data(rom_2_data));
  ROM #(.addrWidth(16), .dataWidth(16)) rom_3 (.addr(counter_1_q), .data(rom_3_data));
  ROM #(.addrWidth(16), .dataWidth(16)) rom_4 (.addr(counter_1_q), .data(rom_4_data));
  Clock clock_2 (.out(clock_2_out));
  Clock clock_3 (.out(clock_3_out));
  PLEX plex_1 (
    .in_1(rom_2_data), .out_2(plex_1_out_2), .out_3(plex_1_out_3), .out_4(plex_1_out_4),
    .out_6(plex_1_out_6), .out_7(plex_1_out_7), .out_8(plex_1_out_8), .out_9(plex_1_out_9));  // open: out_5, out_10
  Register #(.width(16)) register_1 (
    .D(rom_3_data), .en(plex_1_out_4), .clk(clock_2_out), .Q(register_1_q));  // open: clr
  Register #(.width(16)) register_2 (
    .D(rom_4_data), .en(plex_1_out_4), .clk(clock_3_out), .Q(register_2_q));  // open: clr
  or or_1 (or_1_out, plex_1_out_6, plex_1_out_7, plex_1_out_8, plex_1_out_9);
  or or_2 (or_2_out, plex_1_out_3, plex_1_out_2, plex_1_out_4);
  or or_3 (or_3_out, or_2_out, or_1_out);
  ROM #(.addrWidth(16), .dataWidth(16)) rom_5 (.addr(counter_1_q), .data(rom_5_data));
  assign controlled_buffer_1_out = or_3_out ? adder_1_out : 16'bz;  // Controlled_Buffer controlled_buffer_1
  not not_1 (not_1_out, or_3_out);
  assign controlled_buffer_1_out = not_1_out ? {16{1'b0}} : 16'bz;  // Controlled_Buffer controlled_buffer_2
  RAM #(.addrWidth(16), .dataWidth(16)) ram_1 (
    .addr(register_2_q), .we(1'b1), .oe(1'b1), .clk(clock_4_out), .din(controlled_buffer_1_out),
    .dout(ram_1_dout));
  Clock clock_4 (.out(clock_4_out));
  Adder #(.width(16)) adder_1 (.a(register_1_q), .b(ram_1_dout), .out(adder_1_out));  // open: cin, cout
  Comparator #(.width(16)) comparator_1 (
    .a(rom_5_data), .b(adder_1_out), .gt(comparator_1_gt), .lt(comparator_1_lt));  // open: eq
  LED led_1 (.in(comparator_1_gt));
  LED led_2 (.in(comparator_1_lt));

  // Notes on the sheet:
  //   contents of rom_2 (hex, n*v repeats v):
  //   4*2 3 0 0 0 1
  //   contents of rom_3 (hex, n*v repeats v):
  //   1 1 1
  //   contents of rom_4 (hex, n*v repeats v):
  //   8*1
  //   contents of rom_5 (hex, n*v repeats v):
  //   8*1
endmodule

module PC320 (
);

  wire and_1_out, and_2_out, clock_1_out, clock_2_out, clock_3_out, clock_4_out, comparator_1_gt,
       comparator_1_lt, not_1_out, or_1_out, or_2_out, or_3_out, or_4_out, plex_1_out_2, plex_1_out_3,
       plex_1_out_4, plex_1_out_6, plex_1_out_7, plex_1_out_8, plex_1_out_9;
  wire [15:0] adder_1_out, controlled_buffer_1_out, counter_1_q, ram_1_dout, register_1_q, register_2_q,
       rom_1_data, rom_2_data, rom_3_data, rom_4_data, rom_5_data;

  ROM #(.addrWidth(16), .dataWidth(16)) rom_1 (.addr(counter_1_q), .data(rom_1_data));
  Counter #(.max('hffff), .width(16)) counter_1 (
    .load(or_1_out), .clk(clock_1_out), .D(rom_1_data), .Q(counter_1_q));  // open: clr, up, count, carry
  Clock clock_1 (.out(clock_1_out));
  or or_1 (or_1_out, and_1_out, and_2_out, plex_1_out_3);
  ROM #(.addrWidth(16), .dataWidth(16)) rom_2 (.addr(counter_1_q), .data(rom_2_data));
  ROM #(.addrWidth(16), .dataWidth(16)) rom_3 (.addr(counter_1_q), .data(rom_3_data));
  ROM #(.addrWidth(16), .dataWidth(16)) rom_4 (.addr(counter_1_q), .data(rom_4_data));
  Clock clock_2 (.out(clock_2_out));
  Clock clock_3 (.out(clock_3_out));
  PLEX plex_1 (
    .in_1(rom_2_data), .out_2(plex_1_out_2), .out_3(plex_1_out_3), .out_4(plex_1_out_4),
    .out_6(plex_1_out_6), .out_7(plex_1_out_7), .out_8(plex_1_out_8), .out_9(plex_1_out_9));  // open: out_5, out_10
  Register #(.width(16)) register_1 (
    .D(rom_3_data), .en(plex_1_out_4), .clk(clock_2_out), .Q(register_1_q));  // open: clr
  Register #(.width(16)) register_2 (
    .D(rom_4_data), .en(plex_1_out_4), .clk(clock_3_out), .Q(register_2_q));  // open: clr
  and and_1 (and_1_out, comparator_1_lt, plex_1_out_6);
  and and_2 (and_2_out, comparator_1_gt, plex_1_out_7);
  or or_2 (or_2_out, plex_1_out_6, plex_1_out_7, plex_1_out_8, plex_1_out_9);
  or or_3 (or_3_out, plex_1_out_3, plex_1_out_2, plex_1_out_4);
  or or_4 (or_4_out, or_3_out, or_2_out);
  ROM #(.addrWidth(16), .dataWidth(16)) rom_5 (.addr(counter_1_q), .data(rom_5_data));
  assign controlled_buffer_1_out = or_4_out ? adder_1_out : 16'bz;  // Controlled_Buffer controlled_buffer_1
  not not_1 (not_1_out, or_4_out);
  assign controlled_buffer_1_out = not_1_out ? {16{1'b0}} : 16'bz;  // Controlled_Buffer controlled_buffer_2
  RAM #(.addrWidth(16), .dataWidth(16)) ram_1 (
    .addr(register_2_q), .we(1'b1), .oe(1'b1), .clk(clock_4_out), .din(controlled_buffer_1_out),
    .dout(ram_1_dout));
  Clock clock_4 (.out(clock_4_out));
  Adder #(.width(16)) adder_1 (.a(register_1_q), .b(ram_1_dout), .out(adder_1_out));  // open: cin, cout
  Comparator #(.width(16)) comparator_1 (
    .a(rom_5_data), .b(adder_1_out), .gt(comparator_1_gt), .lt(comparator_1_lt));  // open: eq
  LED led_1 (.in(comparator_1_gt));
  LED led_2 (.in(comparator_1_lt));

  // Notes on the sheet:
  //   contents of rom_2 (hex, n*v repeats v):
  //   4*2 3 0 0 0 1
  //   contents of rom_3 (hex, n*v repeats v):
  //   1 1 1
  //   contents of rom_4 (hex, n*v repeats v):
  //   8*1
  //   contents of rom_5 (hex, n*v repeats v):
  //   8*1
endmodule

module PC330 (
);

  wire and_1_out, and_2_out, clock_1_out, clock_2_out, clock_3_out, clock_4_out, comparator_1_gt,
       comparator_1_lt, not_1_out, or_1_out, or_2_out, or_3_out, or_4_out, plex_1_out_2, plex_1_out_3,
       plex_1_out_4, plex_1_out_6, plex_1_out_7, plex_1_out_8, plex_1_out_9;
  wire [15:0] adder_1_out, controlled_buffer_1_out, counter_1_q, ram_1_dout, register_1_q, register_2_q,
       rom_1_data, rom_2_data, rom_3_data, rom_4_data, rom_5_data;

  Clock clock_1 (.out(clock_1_out));
  ROM #(.addrWidth(16), .dataWidth(16)) rom_1 (.addr(counter_1_q), .data(rom_1_data));
  Counter #(.max('hffff), .width(16)) counter_1 (
    .load(or_1_out), .clk(clock_1_out), .D(rom_1_data), .Q(counter_1_q));  // open: clr, up, count, carry
  ROM #(.addrWidth(16), .dataWidth(16)) rom_2 (.addr(counter_1_q), .data(rom_2_data));
  or or_1 (or_1_out, and_1_out, and_2_out, plex_1_out_3);
  ROM #(.addrWidth(16), .dataWidth(16)) rom_3 (.addr(counter_1_q), .data(rom_3_data));
  ROM #(.addrWidth(16), .dataWidth(16)) rom_4 (.addr(counter_1_q), .data(rom_4_data));
  Clock clock_2 (.out(clock_2_out));
  Clock clock_3 (.out(clock_3_out));
  and and_1 (and_1_out, comparator_1_lt, plex_1_out_6);
  and and_2 (and_2_out, comparator_1_gt, plex_1_out_7);
  PLEX plex_1 (
    .in_1(rom_3_data), .out_2(plex_1_out_2), .out_3(plex_1_out_3), .out_4(plex_1_out_4),
    .out_6(plex_1_out_6), .out_7(plex_1_out_7), .out_8(plex_1_out_8), .out_9(plex_1_out_9));  // open: out_5, out_10
  Register #(.width(16)) register_1 (
    .D(rom_2_data), .en(plex_1_out_4), .clk(clock_2_out), .Q(register_1_q));  // open: clr
  Register #(.width(16)) register_2 (
    .D(rom_4_data), .en(plex_1_out_4), .clk(clock_3_out), .Q(register_2_q));  // open: clr
  or or_2 (or_2_out, plex_1_out_6, plex_1_out_7, plex_1_out_8, plex_1_out_9);
  or or_3 (or_3_out, plex_1_out_3, plex_1_out_2, plex_1_out_4);
  ROM #(.addrWidth(16), .dataWidth(16)) rom_5 (.addr(counter_1_q), .data(rom_5_data));
  assign controlled_buffer_1_out = or_4_out ? adder_1_out : 16'bz;  // Controlled_Buffer controlled_buffer_1
  or or_4 (or_4_out, or_3_out, or_2_out);
  assign controlled_buffer_1_out = not_1_out ? {16{1'b0}} : 16'bz;  // Controlled_Buffer controlled_buffer_2
  not not_1 (not_1_out, or_4_out);
  Clock clock_4 (.out(clock_4_out));
  RAM #(.addrWidth(16), .dataWidth(16)) ram_1 (
    .addr(register_2_q), .we(1'b1), .oe(1'b1), .clk(clock_4_out), .din(controlled_buffer_1_out),
    .dout(ram_1_dout));
  Adder #(.width(16)) adder_1 (.a(register_1_q), .b(ram_1_dout), .out(adder_1_out));  // open: cin, cout
  Comparator #(.width(16)) comparator_1 (
    .a(rom_5_data), .b(adder_1_out), .gt(comparator_1_gt), .lt(comparator_1_lt));  // open: eq
  LED led_1 (.in(comparator_1_gt));
  LED led_2 (.in(comparator_1_lt));

  // Notes on the sheet:
  //   contents of rom_2 (hex, n*v repeats v):
  //   1 1 1
  //   contents of rom_3 (hex, n*v repeats v):
  //   4*2 3 0 6 5 1
  //   contents of rom_4 (hex, n*v repeats v):
  //   8*1
  //   contents of rom_5 (hex, n*v repeats v):
  //   8*1
endmodule

module PC335 (
);

  wire and_1_out, and_2_out, clock_1_out, clock_2_out, clock_3_out, clock_4_out, comparator_1_gt,
       comparator_1_lt, not_1_out, or_1_out, or_2_out, or_3_out, or_4_out, plex_1_out_2, plex_1_out_3,
       plex_1_out_4, plex_1_out_6, plex_1_out_7, plex_1_out_8, plex_1_out_9;
  wire [15:0] adder_1_out, controlled_buffer_1_out, counter_1_q, ram_1_dout, register_1_q, register_2_q,
       rom_1_data, rom_2_data, rom_3_data, rom_4_data, rom_5_data;

  ROM #(.addrWidth(16), .dataWidth(16)) rom_1 (.addr(counter_1_q), .data(rom_1_data));
  Counter #(.max('hffff), .width(16)) counter_1 (
    .load(or_1_out), .clk(clock_1_out), .D(rom_1_data), .Q(counter_1_q));  // open: clr, up, count, carry
  Clock clock_1 (.out(clock_1_out));
  or or_1 (or_1_out, and_1_out, and_2_out, plex_1_out_3);
  ROM #(.addrWidth(16), .dataWidth(16)) rom_2 (.addr(counter_1_q), .data(rom_2_data));
  ROM #(.addrWidth(16), .dataWidth(16)) rom_3 (.addr(counter_1_q), .data(rom_3_data));
  ROM #(.addrWidth(16), .dataWidth(16)) rom_4 (.addr(counter_1_q), .data(rom_4_data));
  Clock clock_2 (.out(clock_2_out));
  Clock clock_3 (.out(clock_3_out));
  PLEX plex_1 (
    .in_1(rom_2_data), .out_2(plex_1_out_2), .out_3(plex_1_out_3), .out_4(plex_1_out_4),
    .out_6(plex_1_out_6), .out_7(plex_1_out_7), .out_8(plex_1_out_8), .out_9(plex_1_out_9));  // open: out_5, out_10
  Register #(.width(16)) register_1 (
    .D(rom_3_data), .en(plex_1_out_4), .clk(clock_2_out), .Q(register_1_q));  // open: clr
  Register #(.width(16)) register_2 (
    .D(rom_4_data), .en(plex_1_out_4), .clk(clock_3_out), .Q(register_2_q));  // open: clr
  and and_1 (and_1_out, comparator_1_lt, plex_1_out_6);
  and and_2 (and_2_out, comparator_1_gt, plex_1_out_7);
  or or_2 (or_2_out, plex_1_out_6, plex_1_out_7, plex_1_out_8, plex_1_out_9);
  or or_3 (or_3_out, plex_1_out_3, plex_1_out_2, plex_1_out_4);
  ROM #(.addrWidth(16), .dataWidth(16)) rom_5 (.addr(counter_1_q), .data(rom_5_data));
  assign controlled_buffer_1_out = or_4_out ? adder_1_out : 16'bz;  // Controlled_Buffer controlled_buffer_1
  or or_4 (or_4_out, or_3_out, or_2_out);
  not not_1 (not_1_out, or_4_out);
  Clock clock_4 (.out(clock_4_out));
  assign controlled_buffer_1_out = not_1_out ? {16{1'b0}} : 16'bz;  // Controlled_Buffer controlled_buffer_2
  RAM #(.addrWidth(16), .dataWidth(16)) ram_1 (
    .addr(register_2_q), .we(1'b1), .oe(1'b1), .clk(clock_4_out), .din(controlled_buffer_1_out),
    .dout(ram_1_dout));
  Adder #(.width(16)) adder_1 (.a(register_1_q), .b(ram_1_dout), .out(adder_1_out));  // open: cin, cout
  Comparator #(.width(16)) comparator_1 (
    .a(rom_5_data), .b(adder_1_out), .gt(comparator_1_gt), .lt(comparator_1_lt));  // open: eq
  LED led_1 (.in(comparator_1_gt));
  LED led_2 (.in(comparator_1_lt));

  // Notes on the sheet:
  //   contents of rom_2 (hex, n*v repeats v):
  //   4*2 3 0 6 5 1
  //   contents of rom_3 (hex, n*v repeats v):
  //   1 1 1
  //   contents of rom_4 (hex, n*v repeats v):
  //   8*1
  //   contents of rom_5 (hex, n*v repeats v):
  //   8*1
endmodule

module PC340 (
);

  wire and_1_out, and_2_out, clock_1_out, clock_2_out, clock_3_out, clock_4_out, comparator_1_gt,
       comparator_1_lt, not_1_out, or_1_out, or_2_out, or_3_out, or_4_out, plex_1_out_2, plex_1_out_3,
       plex_1_out_4, plex_1_out_6, plex_1_out_7, plex_1_out_8, plex_1_out_9;
  wire [15:0] adder_1_out, controlled_buffer_1_out, counter_1_q, ram_1_dout, register_1_q, register_2_q,
       rom_1_data, rom_2_data, rom_3_data, rom_4_data, rom_5_data;

  ROM #(.addrWidth(16), .dataWidth(16)) rom_1 (.addr(counter_1_q), .data(rom_1_data));
  Counter #(.max('hffff), .width(16)) counter_1 (
    .load(or_1_out), .clk(clock_1_out), .D(rom_1_data), .Q(counter_1_q));  // open: clr, up, count, carry
  Clock clock_1 (.out(clock_1_out));
  ROM #(.addrWidth(16), .dataWidth(16)) rom_2 (.addr(counter_1_q), .data(rom_2_data));
  ROM #(.addrWidth(16), .dataWidth(16)) rom_3 (.addr(counter_1_q), .data(rom_3_data));
  or or_1 (or_1_out, and_1_out, and_2_out, plex_1_out_3);
  ROM #(.addrWidth(16), .dataWidth(16)) rom_4 (.addr(counter_1_q), .data(rom_4_data));
  PLEX plex_1 (
    .in_1(rom_2_data), .out_2(plex_1_out_2), .out_3(plex_1_out_3), .out_4(plex_1_out_4),
    .out_6(plex_1_out_6), .out_7(plex_1_out_7), .out_8(plex_1_out_8), .out_9(plex_1_out_9));  // open: out_5, out_10
  Register #(.width(16)) register_1 (
    .D(rom_3_data), .en(plex_1_out_4), .clk(clock_2_out), .Q(register_1_q));  // open: clr
  Clock clock_2 (.out(clock_2_out));
  Register #(.width(16)) register_2 (
    .D(rom_4_data), .en(plex_1_out_4), .clk(clock_3_out), .Q(register_2_q));  // open: clr
  Clock clock_3 (.out(clock_3_out));
  and and_1 (and_1_out, comparator_1_lt, plex_1_out_6);
  and and_2 (and_2_out, comparator_1_gt, plex_1_out_7);
  or or_2 (or_2_out, plex_1_out_6, plex_1_out_7, plex_1_out_8, plex_1_out_9);
  or or_3 (or_3_out, plex_1_out_3, plex_1_out_2, plex_1_out_4);
  or or_4 (or_4_out, or_3_out, or_2_out);
  ROM #(.addrWidth(16), .dataWidth(16)) rom_5 (.addr(counter_1_q), .data(rom_5_data));
  assign controlled_buffer_1_out = or_4_out ? adder_1_out : 16'bz;  // Controlled_Buffer controlled_buffer_1
  not not_1 (not_1_out, or_4_out);
  assign controlled_buffer_1_out = not_1_out ? {16{1'b0}} : 16'bz;  // Controlled_Buffer controlled_buffer_2
  RAM #(.addrWidth(16), .dataWidth(16)) ram_1 (
    .addr(register_2_q), .we(1'b1), .oe(1'b1), .clk(clock_4_out), .din(controlled_buffer_1_out),
    .dout(ram_1_dout));
  Clock clock_4 (.out(clock_4_out));
  Adder #(.width(16)) adder_1 (.a(register_1_q), .b(ram_1_dout), .out(adder_1_out));  // open: cin, cout
  Comparator #(.width(16)) comparator_1 (
    .a(rom_5_data), .b(adder_1_out), .gt(comparator_1_gt), .lt(comparator_1_lt));  // open: eq
  LED led_1 (.in(comparator_1_gt));
  LED led_2 (.in(comparator_1_lt));

  // Notes on the sheet:
  //   contents of rom_2 (hex, n*v repeats v):
  //   4*2 3 0 6 5 1
  //   contents of rom_3 (hex, n*v repeats v):
  //   1 1 1
  //   contents of rom_4 (hex, n*v repeats v):
  //   8*1
  //   contents of rom_5 (hex, n*v repeats v):
  //   8*1
endmodule

module PC345 (
);

  wire and_1_out, and_2_out, clock_1_out, clock_2_out, clock_3_out, clock_4_out, comparator_1_gt,
       comparator_1_lt, not_1_out, or_1_out, or_2_out, or_3_out, or_4_out, plex_1_out_2, plex_1_out_3,
       plex_1_out_4, plex_1_out_6, plex_1_out_7, plex_1_out_8, plex_1_out_9;
  wire [15:0] adder_1_out, controlled_buffer_1_out, counter_1_q, ram_1_dout, register_1_q, register_2_q,
       rom_1_data, rom_2_data, rom_3_data, rom_4_data, rom_5_data;

  ROM #(.addrWidth(16), .dataWidth(16)) rom_1 (.addr(counter_1_q), .data(rom_1_data));
  Counter #(.max('hffff), .width(16)) counter_1 (
    .load(or_1_out), .clk(clock_1_out), .D(rom_1_data), .Q(counter_1_q));  // open: clr, up, count, carry
  Clock clock_1 (.out(clock_1_out));
  ROM #(.addrWidth(16), .dataWidth(16)) rom_2 (.addr(counter_1_q), .data(rom_2_data));
  ROM #(.addrWidth(16), .dataWidth(16)) rom_3 (.addr(counter_1_q), .data(rom_3_data));
  or or_1 (or_1_out, and_1_out, and_2_out, plex_1_out_3);
  ROM #(.addrWidth(16), .dataWidth(16)) rom_4 (.addr(counter_1_q), .data(rom_4_data));
  PLEX plex_1 (
    .in_1(rom_2_data), .out_2(plex_1_out_2), .out_3(plex_1_out_3), .out_4(plex_1_out_4),
    .out_6(plex_1_out_6), .out_7(plex_1_out_7), .out_8(plex_1_out_8), .out_9(plex_1_out_9));  // open: out_5, out_10
  Register #(.width(16)) register_1 (
    .D(rom_3_data), .en(plex_1_out_4), .clk(clock_2_out), .Q(register_1_q));  // open: clr
  Clock clock_2 (.out(clock_2_out));
  Register #(.width(16)) register_2 (
    .D(rom_4_data), .en(plex_1_out_4), .clk(clock_3_out), .Q(register_2_q));  // open: clr
  Clock clock_3 (.out(clock_3_out));
  and and_1 (and_1_out, comparator_1_lt, plex_1_out_6);
  and and_2 (and_2_out, comparator_1_gt, plex_1_out_7);
  or or_2 (or_2_out, plex_1_out_6, plex_1_out_7, plex_1_out_8, plex_1_out_9);
  or or_3 (or_3_out, plex_1_out_3, plex_1_out_2, plex_1_out_4);
  or or_4 (or_4_out, or_3_out, or_2_out);
  ROM #(.addrWidth(16), .dataWidth(16)) rom_5 (.addr(counter_1_q), .data(rom_5_data));
  assign controlled_buffer_1_out = or_4_out ? adder_1_out : 16'bz;  // Controlled_Buffer controlled_buffer_1
  not not_1 (not_1_out, or_4_out);
  assign controlled_buffer_1_out = not_1_out ? {16{1'b0}} : 16'bz;  // Controlled_Buffer controlled_buffer_2
  RAM #(.addrWidth(16), .dataWidth(16)) ram_1 (
    .addr(register_2_q), .we(1'b1), .oe(1'b1), .clk(clock_4_out), .din(controlled_buffer_1_out),
    .dout(ram_1_dout));
  Clock clock_4 (.out(clock_4_out));
  Adder #(.width(16)) adder_1 (.a(register_1_q), .b(ram_1_dout), .out(adder_1_out));  // open: cin, cout
  Comparator #(.width(16)) comparator_1 (
    .a(rom_5_data), .b(adder_1_out), .gt(comparator_1_gt), .lt(comparator_1_lt));  // open: eq
  LED led_1 (.in(comparator_1_gt));
  LED led_2 (.in(comparator_1_lt));

  // Notes on the sheet:
  //   contents of rom_2 (hex, n*v repeats v):
  //   4*2 3 0 6 5 1
  //   contents of rom_3 (hex, n*v repeats v):
  //   1 1 1
  //   contents of rom_4 (hex, n*v repeats v):
  //   8*1
  //   contents of rom_5 (hex, n*v repeats v):
  //   8*1
endmodule

module PC350 (
);

  wire and_1_out, and_2_out, clock_1_out, clock_2_out, clock_3_out, clock_4_out, comparator_1_gt,
       comparator_1_lt, not_1_out, or_1_out, or_2_out, or_3_out, or_4_out, plex_1_out_2, plex_1_out_3,
       plex_1_out_4, plex_1_out_6, plex_1_out_7, plex_1_out_8, plex_1_out_9;
  wire [15:0] adder_1_out, controlled_buffer_1_out, counter_1_q, ram_1_dout, register_1_q, register_2_q,
       rom_1_data, rom_2_data, rom_3_data, rom_4_data, rom_5_data;

  ROM #(.addrWidth(16), .dataWidth(16)) rom_1 (.addr(counter_1_q), .data(rom_1_data));
  Counter #(.max('hffff), .width(16)) counter_1 (
    .load(or_1_out), .clk(clock_1_out), .D(rom_1_data), .Q(counter_1_q));  // open: clr, up, count, carry
  Clock clock_1 (.out(clock_1_out));
  or or_1 (or_1_out, and_1_out, and_2_out, plex_1_out_3);
  ROM #(.addrWidth(16), .dataWidth(16)) rom_2 (.addr(counter_1_q), .data(rom_2_data));
  ROM #(.addrWidth(16), .dataWidth(16)) rom_3 (.addr(counter_1_q), .data(rom_3_data));
  ROM #(.addrWidth(16), .dataWidth(16)) rom_4 (.addr(counter_1_q), .data(rom_4_data));
  Clock clock_2 (.out(clock_2_out));
  Clock clock_3 (.out(clock_3_out));
  PLEX plex_1 (
    .in_1(rom_2_data), .out_2(plex_1_out_2), .out_3(plex_1_out_3), .out_4(plex_1_out_4),
    .out_6(plex_1_out_6), .out_7(plex_1_out_7), .out_8(plex_1_out_8), .out_9(plex_1_out_9));  // open: out_5, out_10
  Register #(.width(16)) register_1 (
    .D(rom_3_data), .en(plex_1_out_4), .clk(clock_2_out), .Q(register_1_q));  // open: clr
  Register #(.width(16)) register_2 (
    .D(rom_4_data), .en(plex_1_out_4), .clk(clock_3_out), .Q(register_2_q));  // open: clr
  and and_1 (and_1_out, comparator_1_lt, plex_1_out_6);
  and and_2 (and_2_out, comparator_1_gt, plex_1_out_7);
  or or_2 (or_2_out, plex_1_out_6, plex_1_out_7, plex_1_out_8, plex_1_out_9);
  or or_3 (or_3_out, plex_1_out_3, plex_1_out_2, plex_1_out_4);
  or or_4 (or_4_out, or_3_out, or_2_out);
  ROM #(.addrWidth(16), .dataWidth(16)) rom_5 (.addr(counter_1_q), .data(rom_5_data));
  assign controlled_buffer_1_out = or_4_out ? adder_1_out : 16'bz;  // Controlled_Buffer controlled_buffer_1
  not not_1 (not_1_out, or_4_out);
  assign controlled_buffer_1_out = not_1_out ? {16{1'b0}} : 16'bz;  // Controlled_Buffer controlled_buffer_2
  RAM #(.addrWidth(16), .dataWidth(16)) ram_1 (
    .addr(register_2_q), .we(1'b1), .oe(1'b1), .clk(clock_4_out), .din(controlled_buffer_1_out),
    .dout(ram_1_dout));
  Clock clock_4 (.out(clock_4_out));
  Adder #(.width(16)) adder_1 (.a(register_1_q), .b(ram_1_dout), .out(adder_1_out));  // open: cin, cout
  Comparator #(.width(16)) comparator_1 (
    .a(rom_5_data), .b(adder_1_out), .gt(comparator_1_gt), .lt(comparator_1_lt));  // open: eq
  LED led_1 (.in(comparator_1_gt));
  LED led_2 (.in(comparator_1_lt));

  // Notes on the sheet:
  //   contents of rom_2 (hex, n*v repeats v):
  //   4*2 3 0 6 5 1
  //   contents of rom_3 (hex, n*v repeats v):
  //   1 1 1
  //   contents of rom_4 (hex, n*v repeats v):
  //   8*1
  //   contents of rom_5 (hex, n*v repeats v):
  //   8*1
endmodule

module PC380 (
);

  wire and_1_out, and_2_out, clock_1_out, clock_2_out, clock_3_out, clock_4_out, comparator_1_gt,
       comparator_1_lt, not_1_out, or_1_out, or_2_out, or_3_out, or_4_out, plex_1_out_2, plex_1_out_3,
       plex_1_out_4, plex_1_out_6, plex_1_out_7, plex_1_out_8, plex_1_out_9;
  wire [15:0] adder_1_out, controlled_buffer_1_out, counter_1_q, ram_1_dout, register_1_q, register_2_q,
       rom_1_data, rom_2_data, rom_3_data, rom_4_data, rom_5_data;

  ROM #(.addrWidth(16), .dataWidth(16)) rom_1 (.addr(counter_1_q), .data(rom_1_data));
  Counter #(.max('hffff), .width(16)) counter_1 (
    .load(or_1_out), .clk(clock_1_out), .D(rom_1_data), .Q(counter_1_q));  // open: clr, up, count, carry
  Clock clock_1 (.out(clock_1_out));
  ROM #(.addrWidth(16), .dataWidth(16)) rom_2 (.addr(counter_1_q), .data(rom_2_data));
  ROM #(.addrWidth(16), .dataWidth(16)) rom_3 (.addr(counter_1_q), .data(rom_3_data));
  or or_1 (or_1_out, and_1_out, and_2_out, plex_1_out_3);
  ROM #(.addrWidth(16), .dataWidth(16)) rom_4 (.addr(counter_1_q), .data(rom_4_data));
  PLEX plex_1 (
    .in_1(rom_2_data), .out_2(plex_1_out_2), .out_3(plex_1_out_3), .out_4(plex_1_out_4),
    .out_6(plex_1_out_6), .out_7(plex_1_out_7), .out_8(plex_1_out_8), .out_9(plex_1_out_9));  // open: out_5, out_10
  Register #(.width(16)) register_1 (
    .D(rom_3_data), .en(plex_1_out_4), .clk(clock_2_out), .Q(register_1_q));  // open: clr
  Clock clock_2 (.out(clock_2_out));
  Register #(.width(16)) register_2 (
    .D(rom_4_data), .en(plex_1_out_4), .clk(clock_3_out), .Q(register_2_q));  // open: clr
  Clock clock_3 (.out(clock_3_out));
  and and_1 (and_1_out, comparator_1_lt, plex_1_out_6);
  and and_2 (and_2_out, comparator_1_gt, plex_1_out_7);
  or or_2 (or_2_out, plex_1_out_6, plex_1_out_7, plex_1_out_8, plex_1_out_9);
  or or_3 (or_3_out, plex_1_out_3, plex_1_out_2, plex_1_out_4);
  or or_4 (or_4_out, or_3_out, or_2_out);
  ROM #(.addrWidth(16), .dataWidth(16)) rom_5 (.addr(counter_1_q), .data(rom_5_data));
  assign controlled_buffer_1_out = or_4_out ? adder_1_out : 16'bz;  // Controlled_Buffer controlled_buffer_1
  not not_1 (not_1_out, or_4_out);
  assign controlled_buffer_1_out = not_1_out ? {16{1'b0}} : 16'bz;  // Controlled_Buffer controlled_buffer_2
  RAM #(.addrWidth(16), .dataWidth(16)) ram_1 (
    .addr(register_2_q), .we(1'b1), .oe(1'b1), .clk(clock_4_out), .din(controlled_buffer_1_out),
    .dout(ram_1_dout));
  Clock clock_4 (.out(clock_4_out));
  Adder #(.width(16)) adder_1 (.a(register_1_q), .b(ram_1_dout), .out(adder_1_out));  // open: cin, cout
  Comparator #(.width(16)) comparator_1 (
    .a(rom_5_data), .b(adder_1_out), .gt(comparator_1_gt), .lt(comparator_1_lt));  // open: eq
  LED led_1 (.in(comparator_1_gt));
  LED led_2 (.in(comparator_1_lt));

  // Notes on the sheet:
  //   contents of rom_2 (hex, n*v repeats v):
  //   4*2 3 0 6 5 1
  //   contents of rom_3 (hex, n*v repeats v):
  //   1 1 1
  //   contents of rom_4 (hex, n*v repeats v):
  //   8*1
  //   contents of rom_5 (hex, n*v repeats v):
  //   8*1
endmodule
