// Logisim project MadDrFrankComputerDemo80.circ as structural Verilog: 8 circuits, main circuit main
module main (
);

  wire clock_1_out, plex_1_out_2, plex_1_out_3, plex_1_out_4, plex_1_out_5, plex_1_out_6, plex_1_out_7;
  wire [15:0] adder_1_out, counter_1_q, register_1_q, register_2_q, rom_1_data, rom_2_data, subtractor_1_out;

  Clock clock_1 (.out(clock_1_out));
  Counter #(.max('hffff), .width(16)) counter_1 (
    .load(plex_1_out_3), .clk(clock_1_out), .D(rom_2_data), .Q(counter_1_q));  // open: clr, up, count, carry
  ROM #(.addrWidth(16), .dataWidth(16)) rom_1 (.addr(counter_1_q), .data(rom_1_data));
  ROM #(.addrWidth(16), .dataWidth(16)) rom_2 (.addr(counter_1_q), .data(rom_2_data));
  DotMatrix #(.matrixcols(1), .matrixrows(1)) dotmatrix_1 (.col0(plex_1_out_2));
  PLEX plex_1 (
    .in_1(rom_1_data), .out_2(plex_1_out_2), .out_3(plex_1_out_3), .out_4(plex_1_out_4),
    .out_5(plex_1_out_5), .out_6(plex_1_out_6), .out_7(plex_1_out_7));  // open: out_8, out_9
  Register #(.width(16)) register_1 (
    .D(rom_2_data), .en(plex_1_out_4), .clk(clock_1_out), .Q(register_1_q));  // open: clr
  Register #(.width(16)) register_2 (
    .D(rom_2_data), .en(plex_1_out_5), .clk(clock_1_out), .Q(register_2_q));  // open: clr
  Register #(.width(16)) register_3 (.D(subtractor_1_out), .en(plex_1_out_7), .clk(clock_1_out));  // open: Q, clr
  Subtractor #(.width(16)) subtractor_1 (
    .a(register_1_q), .b(register_2_q), .out(subtractor_1_out));  // open: bin, bout
  Register #(.width(16)) register_4 (.D(adder_1_out), .en(plex_1_out_6), .clk(clock_1_out));  // open: Q, clr
  Adder #(.width(16)) adder_1 (.a(register_1_q), .b(register_2_q), .out(adder_1_out));  // open: cin, cout

  // Notes on the sheet:
  //   contents of rom_1 (hex, n*v repeats v):
  //   2 2 2 3 3 3 4 4 4 5 5 5 6 7 0 0 0 1
  //   contents of rom_2 (hex, n*v repeats v):
  //   1111 2222 5555 1111 2222 4444
endmodule

module PLEX (
  input  [15:0] in_1,
  output out_2,
  output out_3,
  output out_4,
  output out_5,
  output out_6,
  output out_7,
  output out_8,
  output out_9
);

  Comparator #(.width(16)) comparator_1 (.a(in_1), .b({16{1'b0}}), .eq(out_2));  // open: gt, lt
  Comparator #(.width(16)) comparator_2 (.a(in_1), .b(16'h1), .eq(out_3));  // open: gt, lt
  Comparator #(.width(16)) comparator_3 (.a(in_1), .b(16'h2), .eq(out_4));  // open: gt, lt
  Comparator #(.width(16)) comparator_4 (.a(in_1), .b(16'h3), .eq(out_5));  // open: gt, lt
  Comparator #(.width(16)) comparator_5 (.a(in_1), .b(16'h4), .eq(out_6));  // open: gt, lt
  Comparator #(.width(16)) comparator_6 (.a(in_1), .b(16'h5), .eq(out_7));  // open: gt, lt
  Comparator #(.width(16)) comparator_7 (.a(in_1), .b(16'h6), .eq(out_8));  // open: gt, lt
  Comparator #(.width(16)) comparator_8 (.a(in_1), .b(16'h7), .eq(out_9));  // open: gt, lt
endmodule

module ALIMENTATOR (
  input  [15:0] in_1,
  input  in_2,
  output [15:0] out_3
);

  wire clock_1_out;
  wire [15:0] register_1_q, register_2_q;

  Clock clock_1 (.out(clock_1_out));
  Register #(.width(16)) register_1 (.D(in_1), .en(clock_1_out), .clk(clock_1_out), .Q(register_1_q));  // open: clr
  Register #(.width(16)) register_2 (.D(out_3), .en(clock_1_out), .clk(clock_1_out), .Q(register_2_q), .clr(in_2));
  Adder #(.width(16)) adder_1 (.a(register_1_q), .b(register_2_q), .out(out_3));  // open: cin, cout
endmodule

module PC1 (
  input  in_1,
  output [15:0] out_2
);

  wire clock_1_out, comparator_1_eq;
  wire [15:0] counter_1_q, register_1_q, register_2_q, rom_1_data, rom_2_data;

  Clock clock_1 (.out(clock_1_out));
  Counter #(.max('hffff), .width(16)) counter_1 (
    .load(comparator_1_eq), .clk(clock_1_out), .D(rom_1_data), .Q(counter_1_q));  // open: clr, up, count, carry
  ROM #(.addrWidth(16), .dataWidth(16)) rom_1 (.addr(counter_1_q), .data(rom_1_data));
  Register #(.width(16)) register_1 (
    .D(rom_1_data), .en(clock_1_out), .clk(clock_1_out), .Q(register_1_q));  // open: clr
  Register #(.width(16)) register_2 (.D(out_2), .en(clock_1_out), .clk(clock_1_out), .Q(register_2_q), .clr(in_1));
  ROM #(.addrWidth(16), .dataWidth(16)) rom_2 (.addr(counter_1_q), .data(rom_2_data));
  Adder #(.width(16)) adder_1 (.a(register_1_q), .b(register_2_q), .out(out_2));  // open: cin, cout
  Comparator #(.width(16)) comparator_1 (.a(16'h1), .b(rom_2_data), .eq(comparator_1_eq));  // open: gt, lt

  // Notes on the sheet:
  //   contents of rom_1 (hex, n*v repeats v):
  //   1 3 1
  //   contents of rom_2 (hex, n*v repeats v):
  //   0 0 0 1
endmodule

module PC2 (
);

  wire clock_1_out, comparator_1_eq, comparator_2_eq;
  wire [15:0] adder_1_out, counter_1_q, register_1_q, register_2_q, rom_1_data, rom_2_data;

  Counter #(.max('hffff), .width(16)) counter_1 (
    .load(comparator_1_eq), .clk(clock_1_out), .D(rom_1_data), .Q(counter_1_q));  // open: clr, up, count, carry
  Clock clock_1 (.out(clock_1_out));
  ROM #(.addrWidth(16), .dataWidth(16)) rom_1 (.addr(counter_1_q), .data(rom_1_data));
  Register #(.width(16)) register_1 (
    .D(rom_1_data), .en(clock_1_out), .clk(clock_1_out), .Q(register_1_q));  // open: clr
  Register #(.width(16)) register_2 (
    .D(adder_1_out), .en(clock_1_out), .clk(clock_1_out), .Q(register_2_q), .clr(comparator_2_eq));
  ROM #(.addrWidth(16), .dataWidth(16)) rom_2 (.addr(counter_1_q), .data(rom_2_data));
  Adder #(.width(16)) adder_1 (.a(register_1_q), .b(register_2_q), .out(adder_1_out));  // open: cin, cout
  Comparator #(.width(16)) comparator_1 (.a(16'h1), .b(rom_2_data), .eq(comparator_1_eq));  // open: gt, lt
  Comparator #(.width(16)) comparator_2 (.a(16'h2), .b(rom_2_data), .eq(comparator_2_eq));  // open: gt, lt

  // Notes on the sheet:
  //   contents of rom_1 (hex, n*v repeats v):
  //   5*1
  //   contents of rom_2 (hex, n*v repeats v):
  //   5*0 2 1
endmodule

module PC3 (
);

  wire clock_1_out, comparator_1_eq, comparator_2_eq;
  wire [15:0] adder_1_out, counter_1_q, register_1_q, register_2_q, rom_1_data, rom_2_data;

  Clock clock_1 (.out(clock_1_out));
  Counter #(.max('hffff), .width(16)) counter_1 (
    .load(comparator_1_eq), .clk(clock_1_out), .D(rom_1_data), .Q(counter_1_q));  // open: clr, up, count, carry
  ROM #(.addrWidth(16), .dataWidth(16)) rom_1 (.addr(counter_1_q), .data(rom_1_data));
  Register #(.width(16)) register_1 (
    .D(rom_1_data), .en(clock_1_out), .clk(clock_1_out), .Q(register_1_q));  // open: clr
  Register #(.width(16)) register_2 (
    .D(adder_1_out), .en(clock_1_out), .clk(clock_1_out), .Q(register_2_q), .clr(comparator_2_eq));
  ROM #(.addrWidth(16), .dataWidth(16)) rom_2 (.addr(counter_1_q), .data(rom_2_data));
  Adder #(.width(16)) adder_1 (.a(register_1_q), .b(register_2_q), .out(adder_1_out));  // open: cin, cout
  Comparator #(.width(16)) comparator_1 (.a(16'h1), .b(rom_2_data), .eq(comparator_1_eq));  // open: gt, lt
  Comparator #(.width(16)) comparator_2 (.a(16'h2), .b(rom_2_data), .eq(comparator_2_eq));  // open: gt, lt

  // Notes on the sheet:
  //   contents of rom_1 (hex, n*v repeats v):
  //   5*1
  //   contents of rom_2 (hex, n*v repeats v):
  //   5*0 2 1
endmodule

module PC4 (
);

  wire clock_1_out, plex_1_out_3, plex_1_out_4;
  wire [15:0] adder_1_out, counter_1_q, register_1_q, register_2_q, rom_1_data, rom_2_data;

  Clock clock_1 (.out(clock_1_out));
  Counter #(.max('hffff), .width(16)) counter_1 (
    .load(plex_1_out_3), .clk(clock_1_out), .D(rom_1_data), .Q(counter_1_q));  // open: clr, up, count, carry
  ROM #(.addrWidth(16), .dataWidth(16)) rom_1 (.addr(counter_1_q), .data(rom_1_data));
  Register #(.width(16)) register_1 (
    .D(rom_1_data), .en(clock_1_out), .clk(clock_1_out), .Q(register_1_q));  // open: clr
  Register #(.width(16)) register_2 (
    .D(adder_1_out), .en(clock_1_out), .clk(clock_1_out), .Q(register_2_q), .clr(plex_1_out_4));
  ROM #(.addrWidth(16), .dataWidth(16)) rom_2 (.addr(counter_1_q), .data(rom_2_data));
  Adder #(.width(16)) adder_1 (.a(register_1_q), .b(register_2_q), .out(adder_1_out));  // open: cin, cout
  PLEX plex_1 (
    .in_1(rom_2_data), .out_3(plex_1_out_3), .out_4(plex_1_out_4));  // open: out_2, out_5, out_6, out_7, out_8, out_9

  // Notes on the sheet:
  //   contents of rom_1 (hex, n*v repeats v):
  //   5*1
  //   contents of rom_2 (hex, n*v repeats v):
  //   5*0 2 1
endmodule

module PC5 (
);

  wire clock_1_out, plex_1_out_3, plex_1_out_4;
  wire [15:0] adder_1_out, counter_1_q, register_1_q, register_2_q, rom_1_data, rom_2_data;

  Clock clock_1 (.out(clock_1_out));
  Counter #(.max('hffff), .width(16)) counter_1 (
    .load(plex_1_out_3), .clk(clock_1_out), .D(rom_1_data), .Q(counter_1_q));  // open: clr, up, count, carry
  ROM #(.addrWidth(16), .dataWidth(16)) rom_1 (.addr(counter_1_q), .data(rom_1_data));
  Register #(.width(16)) register_1 (
    .D(rom_1_data), .en(clock_1_out), .clk(clock_1_out), .Q(register_1_q));  // open: clr
  Register #(.width(16)) register_2 (
    .D(adder_1_out), .en(clock_1_out), .clk(clock_1_out), .Q(register_2_q), .clr(plex_1_out_4));
  ROM #(.addrWidth(16), .dataWidth(16)) rom_2 (.addr(counter_1_q), .data(rom_2_data));
  Adder #(.width(16)) adder_1 (.a(register_1_q), .b(register_2_q), .out(adder_1_out));  // open: cin, cout
  PLEX plex_1 (
    .in_1(rom_2_data), .out_3(plex_1_out_3), .out_4(plex_1_out_4));  // open: out_2, out_5, out_6, out_7, out_8, out_9

  // Notes on the sheet:
  //   contents of rom_1 (hex, n*v repeats v):
  //   5*1
  //   contents of rom_2 (hex, n*v repeats v):
  //   5*0 2 1
endmodule
