// Logisim project MadDrFrankPCdemo1080.circ as structural Verilog: 2 circuits, main circuit main
module main (
);

  wire clock_1_out, plex_1_out_3;
  wire [15:0] adder_1_out, counter_1_q, ram_1_dout, ram_2_dout, rom_1_data, rom_2_data, rom_3_data,
       rom_4_data, rom_5_data, rom_6_data;

  Counter #(.max('hffff), .width(16)) counter_1 (
    .load(plex_1_out_3), .clk(clock_1_out), .D(rom_2_data), .Q(counter_1_q));  // open: clr, up, count, carry
  Clock clock_1 (.out(clock_1_out));
  ROM #(.addrWidth(16), .dataWidth(16)) rom_1 (.addr(counter_1_q), .data(rom_1_data));
  ROM #(.addrWidth(16), .dataWidth(16)) rom_2 (.addr(counter_1_q), .data(rom_2_data));
  PLEX plex_1 (.in_1(rom_1_data), .out_3(plex_1_out_3));  // open: out_2, out_4, out_5
  RAM #(.addrWidth(16), .dataWidth(16)) ram_1 (
    .addr(rom_3_data), .we(1'b1), .oe(1'b1), .clk(clock_1_out), .din(rom_4_data), .dout(ram_1_dout));
  ROM #(.addrWidth(16), .dataWidth(16)) rom_3 (.addr(counter_1_q), .data(rom_3_data));
  ROM #(.addrWidth(16), .dataWidth(16)) rom_4 (.addr(counter_1_q), .data(rom_4_data));
  RAM #(.addrWidth(16), .dataWidth(16)) ram_2 (
    .addr(rom_5_data), .we(1'b1), .oe(1'b1), .clk(clock_1_out), .din(rom_6_data), .dout(ram_2_dout));
  ROM #(.addrWidth(16), .dataWidth(16)) rom_5 (.addr(counter_1_q), .data(rom_5_data));
  ROM #(.addrWidth(16), .dataWidth(16)) rom_6 (.addr(counter_1_q), .data(rom_6_data));
  Adder #(.width(16)) adder_1 (.a(ram_1_dout), .b(ram_2_dout), .out(adder_1_out));  // open: cin, cout
  RAM #(.addrWidth(2), .dataWidth(16)) ram_3 (
    .addr(2'b00), .we(1'b1), .oe(1'b1), .clk(clock_1_out), .din(adder_1_out));  // open: dout

  // Notes on the sheet:
  //   contents of rom_1 (hex, n*v repeats v):
  //   0 0 1
  //   contents of rom_3 (hex, n*v repeats v):
  //   1 4
  //   contents of rom_4 (hex, n*v repeats v):
  //   1 3
  //   contents of rom_5 (hex, n*v repeats v):
  //   1 4
  //   contents of rom_6 (hex, n*v repeats v):
  //   1 4
endmodule

module PLEX (
  input  [15:0] in_1,
  output out_2,
  output out_3,
  output out_4,
  output out_5
);

  Comparator #(.width(16)) comparator_1 (.a(in_1), .b({16{1'b0}}), .eq(out_2));  // open: gt, lt
  Comparator #(.width(16)) comparator_2 (.a(in_1), .b(16'h1), .eq(out_3));  // open: gt, lt
  Comparator #(.width(16)) comparator_3 (.a(in_1), .b(16'h2), .eq(out_4));  // open: gt, lt
  Comparator #(.width(16)) comparator_4 (.a(in_1), .b(16'h3), .eq(out_5));  // open: gt, lt
endmodule
