// Logisim project MadDrFrankPCdemo250.circ as structural Verilog: 2 circuits, main circuit main
module main (
);

  wire clock_1_out, plexor_1_out_3, plexor_1_out_4, plexor_1_out_5;
  wire [15:0] controlled_buffer_1_out, controlled_buffer_2_out, controlled_buffer_3_out,
       controlled_buffer_4_out, controlled_buffer_5_out, counter_1_q, rom_1_data, rom_2_data, rom_3_data;

  Counter #(.max('hffff), .width(16)) counter_1 (
    .load(plexor_1_out_3), .clk(clock_1_out), .D(controlled_buffer_1_out), .Q(counter_1_q));  // open: clr, up, count, carry
  Clock clock_1 (.out(clock_1_out));
  ROM #(.addrWidth(16), .dataWidth(16)) rom_1 (.addr(counter_1_q), .data(rom_1_data));
  ROM #(.addrWidth(16), .dataWidth(16)) rom_2 (.addr(counter_1_q), .data(rom_2_data));
  plexor plexor_1 (
    .in_1(rom_1_data), .out_3(plexor_1_out_3), .out_4(plexor_1_out_4), .out_5(plexor_1_out_5));  // open: out_2, out_6, out_7, out_8, out_9, out_10, out_11
  assign controlled_buffer_1_out = plexor_1_out_3 ? rom_2_data : 16'bz;  // Controlled_Buffer controlled_buffer_1
  ROM #(.addrWidth(16), .dataWidth(16)) rom_3 (.addr(counter_1_q), .data(rom_3_data));
  assign controlled_buffer_2_out = plexor_1_out_4 ? rom_2_data : 16'bz;  // Controlled_Buffer controlled_buffer_2
  assign controlled_buffer_3_out = plexor_1_out_4 ? rom_3_data : 16'bz;  // Controlled_Buffer controlled_buffer_3
  RAM #(.addrWidth(16), .dataWidth(16)) ram_1 (
    .addr(controlled_buffer_2_out), .we(1'b1), .oe(1'b1), .clk(clock_1_out), .din(controlled_buffer_3_out));  // open: dout
  assign controlled_buffer_4_out = plexor_1_out_5 ? rom_2_data : 16'bz;  // Controlled_Buffer controlled_buffer_4
  assign controlled_buffer_5_out = plexor_1_out_5 ? rom_3_data : 16'bz;  // Controlled_Buffer controlled_buffer_5
  RAM #(.addrWidth(16), .dataWidth(16)) ram_2 (
    .addr(controlled_buffer_4_out), .we(1'b1), .oe(1'b1), .clk(clock_1_out), .din(controlled_buffer_5_out));  // open: dout

  // Notes on the sheet:
  //   contents of rom_1 (hex, n*v repeats v):
  //   0 0 2 2 3 3 0 0 1
  //   contents of rom_2 (hex, n*v repeats v):
  //   0 0 4*100
  //   contents of rom_3 (hex, n*v repeats v):
  //   0 0 1 2 3 4
endmodule

// PLEX
module plexor (
  input  [15:0] in_1,
  output out_2,
  output out_3,
  output out_4,
  output out_5,
  output out_6,
  output out_7,
  output out_8,
  output out_9,
  output out_10,
  output out_11
);

  Comparator #(.width(16)) comparator_1 (.a(in_1), .b({16{1'b0}}), .eq(out_2));  // open: gt, lt
  Comparator #(.width(16)) comparator_2 (.a(in_1), .b(16'h1), .eq(out_3));  // open: gt, lt
  Comparator #(.width(16)) comparator_3 (.a(in_1), .b(16'h2), .eq(out_4));  // open: gt, lt
  Comparator #(.width(16)) comparator_4 (.a(in_1), .b(16'h3), .eq(out_5));  // open: gt, lt
  Comparator #(.width(16)) comparator_5 (.a(in_1), .b(16'h4), .eq(out_6));  // open: gt, lt
  Comparator #(.width(16)) comparator_6 (.a(in_1), .b(16'h5), .eq(out_7));  // open: gt, lt
  Comparator #(.width(16)) comparator_7 (.a(in_1), .b(16'h6), .eq(out_8));  // open: gt, lt
  Comparator #(.width(16)) comparator_8 (.a(in_1), .b(16'h7), .eq(out_9));  // open: gt, lt
  Comparator #(.width(16)) comparator_9 (.a(in_1), .b(16'h8), .eq(out_10));  // open: gt, lt
  Comparator #(.width(16)) comparator_10 (.a(in_1), .b(16'h9), .eq(out_11));  // open: gt, lt
endmodule
