// Logisim project chipDibujadorDeBitsV1000.circ as structural Verilog: 2 circuits, main circuit main
module main (
);

  wire button_1_out, button_2_out, clock_1_out, controlled_buffer_1_out;
  wire [5:0] counter_1_q;
  wire [6:0] mostrador_de_car_cteres_44b09ee2_1_out_2, mostrador_de_car_cteres_44b09ee2_1_out_3,
       mostrador_de_car_cteres_44b09ee2_1_out_4, mostrador_de_car_cteres_44b09ee2_1_out_5,
       mostrador_de_car_cteres_44b09ee2_1_out_6;

  Clock clock_1 (.out(clock_1_out));
  assign controlled_buffer_1_out = button_1_out ? clock_1_out : 1'bz;  // Controlled_Buffer controlled_buffer_1
  Button button_1 (.out(button_1_out));
  Button button_2 (.out(button_2_out));
  Counter #(.max('h3f), .width(6)) counter_1 (
    .clr(button_2_out), .up(button_1_out), .count(1'b1), .clk(controlled_buffer_1_out), .Q(counter_1_q));  // open: load, D, carry
  DotMatrix dotmatrix_1 (
    .col0(mostrador_de_car_cteres_44b09ee2_1_out_6), .col1(mostrador_de_car_cteres_44b09ee2_1_out_5),
    .col2(mostrador_de_car_cteres_44b09ee2_1_out_4), .col3(mostrador_de_car_cteres_44b09ee2_1_out_3),
    .col4(mostrador_de_car_cteres_44b09ee2_1_out_2));
  Mostrador_de_car_cteres_44b09ee2 mostrador_de_car_cteres_44b09ee2_1 (
    .in_1(counter_1_q), .out_2(mostrador_de_car_cteres_44b09ee2_1_out_2),
    .out_3(mostrador_de_car_cteres_44b09ee2_1_out_3), .out_4(mostrador_de_car_cteres_44b09ee2_1_out_4),
    .out_5(mostrador_de_car_cteres_44b09ee2_1_out_5), .out_6(mostrador_de_car_cteres_44b09ee2_1_out_6));
endmodule

// ROM
module Mostrador_de_car_cteres_44b09ee2 (
  input  [5:0] in_1,
  output [6:0] out_2,
  output [6:0] out_3,
  output [6:0] out_4,
  output [6:0] out_5,
  output [6:0] out_6
);

  ROM #(.addrWidth(6), .dataWidth(7)) rom_1 (.addr(in_1), .data(out_2));
  ROM #(.addrWidth(6), .dataWidth(7)) rom_2 (.addr(in_1), .data(out_3));
  ROM #(.addrWidth(6), .dataWidth(7)) rom_3 (.addr(in_1), .data(out_4));
  ROM #(.addrWidth(6), .dataWidth(7)) rom_4 (.addr(in_1), .data(out_5));
  ROM #(.addrWidth(6), .dataWidth(7)) rom_5 (.addr(in_1), .data(out_6));

  // Notes on the sheet:
  //   contents of rom_2 (hex, n*v repeats v):
  //   3e 3e 3a 3e 3e 2e 2e 3e 3e 3e 8 8 14 0 14 3e e 22 3e 2a 28 2e 3e 22 20 2 3e e 2e 36 e 38 3e 3e 3c 3e
  //   16 24 36 20 38 32 0 1c 0 4
  //   contents of rom_3 (hex, n*v repeats v):
  //   22 20 2a 2a 8 2a 2a 20 2a 2a 1c 8 8 14 14 28 a 22 a 2a 28 22 8 3e 3e 2 18 8 28 8 a 28 28 2 2 c 28 2a
  //   8 3e e 2a 22 22 2 2
  //   contents of rom_4 (hex, n*v repeats v):
  //   3e 0 2e 2a 38 3a 3e 20 3e 3a 8 8 14 0 14 3e 3e 3e e 4*3e 22 22 3e 3e e 2e 3e e 3e 38 3e 3c 3e 3e 12
  //   36 20 38 26 1c
endmodule
