// Logisim project dibujador de bits v222.circ as structural Verilog: 1 circuit, main circuit main
module main (
);

  wire button_1_out, clock_1_out, controlled_buffer_1_out;
  wire [5:0] counter_1_q;
  wire [6:0] rom_1_data, rom_2_data, rom_3_data, rom_4_data, rom_5_data;

  Clock clock_1 (.out(clock_1_out));
  assign controlled_buffer_1_out = button_1_out ? clock_1_out : 1'bz;  // Controlled_Buffer controlled_buffer_1
  Button button_1 (.out(button_1_out));
  Counter #(.width(6), .max('h3f)) counter_1 (
    .Q(counter_1_q), .clk(controlled_buffer_1_out));  // open: load, D, count, carry, clr
  ROM #(.addrWidth(6), .dataWidth(7)) rom_1 (.addr(counter_1_q), .data(rom_1_data));  // open: sel
  ROM #(.addrWidth(6), .dataWidth(7)) rom_2 (.addr(counter_1_q), .data(rom_2_data));  // open: sel
  ROM #(.addrWidth(6), .dataWidth(7)) rom_3 (.addr(counter_1_q), .data(rom_3_data));  // open: sel
  ROM #(.addrWidth(6), .dataWidth(7)) rom_4 (.addr(counter_1_q), .data(rom_4_data));  // open: sel
  ROM #(.addrWidth(6), .dataWidth(7)) rom_5 (.addr(counter_1_q), .data(rom_5_data));  // open: sel
  DotMatrix dotmatrix_1 (.col0(rom_5_data), .col1(rom_4_data), .col2(rom_3_data), .col3(rom_2_data), .col4(rom_1_data));

  // Notes on the sheet:
  //   contents of rom_2 (hex, n*v repeats v):
  //   3e 3e 3a 3e 3e 2e 2e 3e 3e 3e 8 8 14 0 14 3e e 22 3e 2a 28 2e 3e 22 20 2 3e e 2e 36 e 38 3e 3e 3c 3e
  //   16 24 36 20 38 32 0 1c 0 4
  //   contents of rom_3 (hex, n*v repeats v):
  //   22 20 2a 2a 8 2a 2a 20 2a 2a 1c 8 8 14 14 28 a 22 a 2a 28 22 8 3e 3e 2 18 8 28 8 a 28 28 2 2 c 28 2a
  //   8 3e e 2a 22 22 2 2
  //   contents of rom_4 (hex, n*v repeats v):
  //   3e 0 2e 2a 38 3a 3e 20 3e 3a 8 8 14 0 14 3e 3e 3e e 4*3e 22 22 3e 3e e 2e 3e e 3e 38 3e 3c 3e 3e 12
  //   36 20 38 26 1c
endmodule
