// Logisim project dibujador de bits v50.circ as structural Verilog: 1 circuit, main circuit main
module main (
);

  wire clock_1_out;
  wire [6:0] rom_1_data, rom_2_data, rom_3_data, rom_4_data, rom_5_data;
  wire [9:0] counter_1_q;

  Clock clock_1 (.out(clock_1_out));
  Counter #(.width(10), .max('h3ff)) counter_1 (
    .Q(counter_1_q), .clk(clock_1_out));  // open: load, D, count, carry, clr
  ROM #(.addrWidth(10), .dataWidth(7)) rom_1 (.addr(counter_1_q), .data(rom_1_data));  // open: sel
  ROM #(.addrWidth(10), .dataWidth(7)) rom_2 (.addr(counter_1_q), .data(rom_2_data));  // open: sel
  ROM #(.addrWidth(10), .dataWidth(7)) rom_3 (.addr(counter_1_q), .data(rom_3_data));  // open: sel
  ROM #(.addrWidth(10), .dataWidth(7)) rom_4 (.addr(counter_1_q), .data(rom_4_data));  // open: sel
  ROM #(.addrWidth(10), .dataWidth(7)) rom_5 (.addr(counter_1_q), .data(rom_5_data));  // open: sel
  DotMatrix dotmatrix_1 (.col0(rom_5_data), .col1(rom_4_data), .col2(rom_3_data), .col3(rom_2_data), .col4(rom_1_data));

  // Notes on the sheet:
  //   contents of rom_2 (hex, n*v repeats v):
  //   3e 3e 3a 3e 3e 2e 2e 3e 3e 3e 8 8 14 0 14 3e
  //   contents of rom_3 (hex, n*v repeats v):
  //   22 20 2a 2a 8 2a 2a 20 2a 2a 1c 8 8 14 14 28
  //   contents of rom_4 (hex, n*v repeats v):
  //   3e 0 2e 2a 38 3a 3e 20 3e 3a 8 8 14 0 14 3e
endmodule
